# Fritzing sketch AdruinoPWM-BLC (saved by Fritzing 0.9.3b)
breadboards: 1

parts:
  M4 = ESC
  920KV_Motor4 = DJI 920 KV Motor
  Bauteil2 = Arduino Micro (Rev3)  # not connected
  R3 = Rotary Potentiometer (Small) [maximum_resistance=100kΩ package=THT]
  Power_plug2 = Power plug

nets:
  N1: M4.U, 920KV_Motor4.u
  N2: M4.V, 920KV_Motor4.v
  N3: M4.W, 920KV_Motor4.w
  GND: M4.GND, R3.leg2, Power_plug2.GND

notes:
  RL CCW
  Rear Left
  12V

custom parts:
  DJI 920 KV Motor: DJI Brushless Outrunner 2212/920K Motor F330-550
