# Fritzing sketch AdruinoPWM-Oszi (saved by Fritzing 0.9.3b)
breadboards: 1

parts:
  Bauteil1 = Arduino Micro (Rev3)  # not connected
  R2 = Rotary Potentiometer (Small) [maximum_resistance=100kΩ package=THT]
  Power_plug1 = Power plug

nets:
  N1: R2.leg2, Power_plug1.GND

notes:
  12V
  PWM OSZI Messung
