# Fritzing sketch Verzögerungsschaltung (saved by Fritzing 0.9.3b)
breadboards: 1

parts:
  U2 = CD4541BE [part_number=CD4541BE package="DIP14 [THT]"]
  R1 = Resistor [tolerance=±5% resistance=1k package="2010 [SMD]"]
  R2 = Resistor [tolerance=±5% resistance=100k package="2010 [SMD]"]
  R3 = Resistor [tolerance=±5% resistance=4.7k package="2010 [SMD]"]
  R4 = Resistor [tolerance=±5% resistance=4.7k package="2010 [SMD]"]
  C2 = Electrolytic Capacitor [capacitance=100µF package="200 mil [THT, electrolytic]"]
  C3 = Ceramic Capacitor [capacitance=100nF package="200 mil [THT, multilayer]"]
  C4 = Ceramic Capacitor [capacitance=150nF package="200 mil [THT, multilayer]"]
  D1 = Diode [package=diode-1n4148]
  D2 = Diode [package=diode-1n4148]
  LED1 = smd LED [color="Red (633nm)" package="0805 [SMD]"]
  Q1 = NPN-Transistor [part_number=BC548 package="TO92 [THT]"]
  R5 = Rotary Potentiometer (Small) [maximum_resistance=100kΩ package=THT]
  OMRON1 = OMRON PCB Power Relay – G5LE [part_number="G5LE-1\n" package=THT]

nets:
  N1: U2.RTC, R1.Pin_1
  N2: U2.CTC, C4.1
  N3: U2.RS, R2.Pin_1
  N4: U2.04, U2.RES
  N5: U2.Q, R4.Pin_0
  N6: U2.Q/Q, U2.MO, U2.A, U2.B
  N7: R1.Pin_0, R5.leg2
  N8: R2.Pin_0, C4.0, R5.leg1, R5.wiper
  N9: R3.Pin_0, D2.A, Q1.E, OMRON1.COIL1
  N10: R3.Pin_1, LED1.cathode
  N11: R4.Pin_1, Q1.C
  N12: C2.-, C3.0, Q1.B
  N13: C3.1, D1.C, D2.C, LED1.anode, OMRON1.COIL2

notes:
  IC TI CD4541BE

custom parts:
  CD4541BE: Quad 2 input NOR logic gates
