# Fritzing sketch NE555-PWM (saved by Fritzing 0.9.3b)
breadboards: 1

parts:
  IC1 = General purpose bipolar Timer [package=dil-08]
  C1 = Ceramic Capacitor [capacitance=100nF package="200 mil [THT, multilayer]"]
  C2 = Ceramic Capacitor [capacitance=10nF package="200 mil [THT, multilayer]"]
  C3 = Ceramic Capacitor [capacitance=10nF package="200 mil [THT, multilayer]"]
  R1 = Resistor [tolerance=±5% resistance=4.7k package="0603 [SMD]"]
  R2 = Resistor [tolerance=±5% resistance=4.7k package="0603 [SMD]"]
  R3 = Resistor [tolerance=±5% resistance=10k package="0603 [SMD]"]
  R4 = Resistor [tolerance=±5% resistance=1k package="0603 [SMD]"]
  R5 = Trimmer Potentiometer [maximum_resistance=1MΩ package=THT]
  LED1 = LED - 5mm [color="Red (633nm)" package="5 mm [THT]"]
  D2 = Diode [package=diode-1n4148]
  D3 = Diode [package=diode-1n4148]  # not connected
  J1 = Power Jack [package=power_jack_slot]

nets:
  GND: IC1.GND, IC1.OUT, C1.1, C2.1, C3.1, R4.Pin_1, LED1.anode, J1.GND
  N1: IC1.TRI, IC1.TRE, C2.0, R5.wiper
  N2: IC1._RES, R3.Pin_1
  N3: IC1.CON, C3.0
  N4: IC1.DIS, R1.Pin_1, R2.Pin_1
  N5: IC1.VCC+, C1.0, R2.Pin_0, R3.Pin_0, J1.PWR
  N6: R1.Pin_0, D2.C
  N7: R4.Pin_0, LED1.cathode

notes:
  NE555 PWM
  https://elektro.turanis.de/html/prj197/index.html
  9V
