// Logisim project computer74.circ as structural Verilog: 10 circuits, main circuit COMPUTER74
module COMPUTER74 (
  input  [11:0] SRCREG,
  input  [11:0] DSTREG,
  input  [11:0] SR,
  input  HALT,
  input  RUN,
  input  START,
  input  SSTEP,
  input  RESET,
  output [11:0] SRC,
  output [11:0] DST,
  output [11:0] DATA,
  output [11:0] SRANZ,
  output [11:0] PC,
  output [23:0] RR,
  output [11:0] R2,
  output [11:0] R3,
  output CO,
  output GL,
  output [5:0] UPC,
  output HLTFF,
  output SRCENB,
  output DSTENB
);

  wire clock_1_out, halt_1_hrst, or_1_out, or_3_out, or_4_out, programmzaehler_1_drdy,
       programmzaehler_1_srdy, rechenwerk_1_drdy, rechenwerk_1_srdy, speicher_1_drdy, speicher_1_srdy,
       steuerwerk_1_dstff, steuerwerk_1_sstpff, steuerwerk_1_strtff, switchreg_1_drdy, switchreg_1_srdy;
  wire [11:0] programmzaehler_1_dout, rechenwerk_1_dout, speicher_1_dout, switchreg_1_dout;

  Clock #(.highDuration(1), .lowDuration(1)) clock_1 (.out(clock_1_out));
  HALT halt_1 (.SRC(SRC), .SRCENB(SRCENB), .HRST(halt_1_hrst));
  or or_1 (or_1_out, RESET, halt_1_hrst);
  STEUERWERK steuerwerk_1 (
    .CLK(clock_1_out), .RST(or_1_out), .SRCREG(SRCREG), .DSTREG(DSTREG), .DATA(DATA), .SRCRDY(or_3_out),
    .DSTRDY(or_4_out), .SRCCMD(1'b0), .DSTCMD(1'b0), .HALT(HALT), .RUN(RUN), .START(START), .SSTEP(SSTEP),
    .SRC(SRC), .DST(DST), .SRCENB(SRCENB), .DSTENB(DSTENB), .UPC(UPC), .HLTFF(HLTFF),
    .DSTFF(steuerwerk_1_dstff), .STRTFF(steuerwerk_1_strtff), .SSTPFF(steuerwerk_1_sstpff));
  SPEICHER speicher_1 (
    .SRC(SRC), .DST(DST), .SRCENB(SRCENB), .DSTENB(DSTENB), .DATA(DATA), .CLK(clock_1_out), .RST(or_1_out),
    .DOUT(speicher_1_dout), .SRDY(speicher_1_srdy), .DRDY(speicher_1_drdy));
  PROGRAMMZAEHLER programmzaehler_1 (
    .SRC(SRC), .DST(DST), .SRCENB(SRCENB), .DSTENB(DSTENB), .DATA(DATA), .CLK(clock_1_out), .RST(or_1_out),
    .DOUT(programmzaehler_1_dout), .SRDY(programmzaehler_1_srdy), .DRDY(programmzaehler_1_drdy), .PC(PC));
  SWITCHREG switchreg_1 (
    .SRC(SRC), .DST(DST), .SRCENB(SRCENB), .DSTENB(DSTENB), .DATA(DATA), .SR(SR), .CLK(clock_1_out),
    .RST(or_1_out), .DOUT(switchreg_1_dout), .SRDY(switchreg_1_srdy), .DRDY(switchreg_1_drdy), .SRANZ(SRANZ));
  RECHENWERK rechenwerk_1 (
    .SRC(SRC), .DST(DST), .SRCENB(SRCENB), .DSTENB(DSTENB), .DATA(DATA), .CLK(clock_1_out), .RST(or_1_out),
    .DOUT(rechenwerk_1_dout), .SRDY(rechenwerk_1_srdy), .DRDY(rechenwerk_1_drdy), .RR(RR), .R2(R2), .R3(R3),
    .CO(CO), .GL(GL));
  assign DATA = speicher_1_dout | programmzaehler_1_dout | switchreg_1_dout | rechenwerk_1_dout;  // OR_Gate or_2, 12 bits wide
  or or_3 (or_3_out, speicher_1_srdy, programmzaehler_1_srdy, switchreg_1_srdy, rechenwerk_1_srdy);
  or or_4 (or_4_out, speicher_1_drdy, programmzaehler_1_drdy, switchreg_1_drdy, rechenwerk_1_drdy);

  // Notes on the sheet:
  //   COMPUTER74
  //   RESET
  //   SSTEP
  //   START
  //   RUN
  //   HALT
  //   SR
  //   DSTREG
  //   SRCREG
  //   Takt
  //   CLK
  //   HALT 7777
  //   SRC
  //   SRCENB
  //   RESET-Leitung
  //   HRST
  //   RST
  //   DATA
  //   SRCRDY
  //   DSTRDY
  //   STEUERWERK
  //   DST
  //   DSTENB
  //   HLTFF
  //   UPC
  //   SPEICHER 0000-1777
  //   dMr
  //   sM
  //   dM
  //   PC 7776
  //   PC
  //   dPr
  //   sP
  //   dP
  //   SR 7774
  //   SRANZ
  //   dSr
  //   sS
  //   dS
  //   RECHENWERK 7700-7767
  //   GL
  //   CO
  //   R3
  //   R2
  //   RR
  //   dRr
  //   sR
  //   dR
  //   DATA (wired-OR)
  //   SRCRDY
  //   DSTRDY
endmodule

module STEUERWERK (
  input  CLK,
  input  RST,
  input  [11:0] SRCREG,
  input  [11:0] DSTREG,
  input  [11:0] DATA,
  input  SRCRDY,
  input  DSTRDY,
  input  SRCCMD,
  input  DSTCMD,
  input  HALT,
  input  RUN,
  input  START,
  input  SSTEP,
  output [11:0] SRC,
  output [11:0] DST,
  output SRCENB,
  output DSTENB,
  output [5:0] UPC,
  output HLTFF,
  output DSTFF,
  output STRTFF,
  output SSTPFF
);

  wire adder_1_cout, and_1_out, and_2_out, and_3_out, and_4_out, and_5_out, and_6_out, d_ff_1_q, d_ff_1_qn,
       d_ff_2_q, d_ff_2_qn, d_ff_3_q, d_ff_3_qn, d_ff_4_q, d_ff_4_qn, demultiplexer_1_out0,
       demultiplexer_1_out1, demultiplexer_1_out2, demultiplexer_1_out3, demultiplexer_1_out6,
       demultiplexer_1_out7, demultiplexer_1_out8, demultiplexer_1_out9, demultiplexer_1_out10,
       demultiplexer_1_out11, demultiplexer_1_out12, demultiplexer_1_out13, demultiplexer_1_out14,
       demultiplexer_1_out15, j_k_ff_1_qn, j_k_ff_2_qn, j_k_ff_3_qn, j_k_ff_4_qn, j_k_ff_5_qn, j_k_ff_6_qn,
       multiplexer_1_out, not_1_out, not_2_out, not_3_out, or_1_out, or_2_out, or_3_out, or_4_out, xnor_1_out;
  wire [1:0] demultiplexer_1_out4;
  wire [5:0] adder_1_out, multiplexer_2_out, multiplexer_3_out;
  wire [11:0] multiplexer_4_out, multiplexer_5_out, multiplexer_6_out, register_2_q, register_3_q, rom_1_data;

  D_Flip_Flop d_ff_1 (.clk(CLK), .D(HALT), .Q(d_ff_1_q), .Qn(d_ff_1_qn));  // open: preset, en, reset
  and and_1 (and_1_out, HALT, d_ff_1_qn);
  D_Flip_Flop d_ff_2 (.clk(CLK), .D(RUN), .Q(d_ff_2_q), .Qn(d_ff_2_qn));  // open: preset, en, reset
  and and_2 (and_2_out, RUN, d_ff_2_qn);
  D_Flip_Flop d_ff_3 (.clk(CLK), .D(START), .Q(d_ff_3_q), .Qn(d_ff_3_qn));  // open: preset, en, reset
  and and_3 (and_3_out, START, d_ff_3_qn);
  D_Flip_Flop d_ff_4 (.clk(CLK), .D(SSTEP), .Q(d_ff_4_q), .Qn(d_ff_4_qn));  // open: preset, en, reset
  and and_4 (and_4_out, SSTEP, d_ff_4_qn);
  Register #(.width(6)) register_1 (.D(multiplexer_3_out), .Q(UPC), .clk(CLK), .clr(RST));  // open: en
  ROM #(.addrWidth(6), .dataWidth(12)) rom_1 (.addr(UPC), .data(rom_1_data));  // open: sel
  Multiplexer #(.select(3), .width(1), .enable("false")) multiplexer_1 (
    .in0(SRCRDY), .in1(DSTRDY), .in2(HLTFF), .in3(DSTFF), .in4(STRTFF), .in5(SSTPFF), .in6(SRCCMD),
    .in7(DSTCMD), .out(multiplexer_1_out), .sel(rom_1_data[5:3]));
  xnor xnor_1 (xnor_1_out, multiplexer_1_out, rom_1_data[2]);
  not not_1 (not_1_out, xnor_1_out);
  not not_2 (not_2_out, rom_1_data[1]);
  not not_3 (not_3_out, rom_1_data[0]);
  or or_1 (or_1_out, not_2_out, xnor_1_out);
  and and_5 (and_5_out, rom_1_data[0], or_1_out);
  and and_6 (and_6_out, not_3_out, rom_1_data[1], not_1_out);
  Adder #(.width(6)) adder_1 (.a(UPC), .b({6{1'b0}}), .out(adder_1_out), .cin(1'b1), .cout(adder_1_cout));
  Multiplexer #(.select(1), .width(6), .enable("false")) multiplexer_2 (
    .in0(adder_1_out), .in1(UPC), .out(multiplexer_2_out), .sel(and_6_out));
  Multiplexer #(.select(1), .width(6), .enable("false")) multiplexer_3 (
    .in0(multiplexer_2_out), .in1(rom_1_data[11:6]), .out(multiplexer_3_out), .sel(and_5_out));
  Demultiplexer #(.select(4), .width(1), .enable("false")) demultiplexer_1 (
    .out0(demultiplexer_1_out0), .out1(demultiplexer_1_out1), .out2(demultiplexer_1_out2),
    .out3(demultiplexer_1_out3), .out4(demultiplexer_1_out4[0]), .out5(demultiplexer_1_out4[1]),
    .out6(demultiplexer_1_out6), .out7(demultiplexer_1_out7), .out8(demultiplexer_1_out8),
    .out9(demultiplexer_1_out9), .out10(demultiplexer_1_out10), .out11(demultiplexer_1_out11),
    .out12(demultiplexer_1_out12), .out13(demultiplexer_1_out13), .out14(demultiplexer_1_out14),
    .out15(demultiplexer_1_out15), .in(not_3_out), .sel(rom_1_data[9:6]));
  or or_2 (or_2_out, demultiplexer_1_out0, demultiplexer_1_out1);
  Multiplexer #(.select(1), .width(12), .enable("false")) multiplexer_4 (
    .in0(DATA), .in1(SRCREG), .out(multiplexer_4_out), .sel(demultiplexer_1_out1));
  Register #(.width(12)) register_2 (.D(multiplexer_4_out), .en(or_2_out), .Q(register_2_q), .clk(CLK));  // open: clr
  Register #(.width(12)) register_3 (.D(DATA), .en(demultiplexer_1_out2), .Q(register_3_q), .clk(CLK));  // open: clr
  or or_3 (or_3_out, demultiplexer_1_out3, demultiplexer_1_out4[0], demultiplexer_1_out4[1]);
  Multiplexer #(.select(2), .width(12), .enable("false")) multiplexer_5 (
    .in0(register_3_q), .in1(register_2_q), .in2(12'hffe), .in3({12{1'b0}}), .out(multiplexer_5_out),
    .sel(demultiplexer_1_out4));
  Register #(.width(12)) register_4 (.D(multiplexer_5_out), .en(or_3_out), .Q(SRC), .clk(CLK));  // open: clr
  or or_4 (or_4_out, demultiplexer_1_out8, demultiplexer_1_out9);
  Multiplexer #(.select(1), .width(12), .enable("false")) multiplexer_6 (
    .in0(DATA), .in1(DSTREG), .out(multiplexer_6_out), .sel(demultiplexer_1_out9));
  Register #(.width(12)) register_5 (.D(multiplexer_6_out), .en(or_4_out), .Q(DST), .clk(CLK));  // open: clr
  J_K_Flip_Flop j_k_ff_1 (
    .J(demultiplexer_1_out6), .clk(CLK), .K(demultiplexer_1_out7), .Q(SRCENB), .Qn(j_k_ff_1_qn), .reset(RST));  // open: preset, en
  J_K_Flip_Flop j_k_ff_2 (
    .J(demultiplexer_1_out10), .clk(CLK), .K(demultiplexer_1_out11), .Q(DSTENB), .Qn(j_k_ff_2_qn), .reset(RST));  // open: preset, en
  J_K_Flip_Flop j_k_ff_3 (
    .J(demultiplexer_1_out12), .clk(CLK), .K(demultiplexer_1_out13), .Q(DSTFF), .Qn(j_k_ff_3_qn), .reset(RST));  // open: preset, en
  J_K_Flip_Flop j_k_ff_4 (
    .J(and_3_out), .clk(CLK), .K(demultiplexer_1_out14), .Q(STRTFF), .Qn(j_k_ff_4_qn));  // open: preset, en, reset
  J_K_Flip_Flop j_k_ff_5 (
    .J(and_4_out), .clk(CLK), .K(demultiplexer_1_out15), .Q(SSTPFF), .Qn(j_k_ff_5_qn));  // open: preset, en, reset
  J_K_Flip_Flop j_k_ff_6 (
    .J(and_1_out), .clk(CLK), .K(and_2_out), .Q(HLTFF), .Qn(j_k_ff_6_qn), .preset(RST));  // open: en, reset

  // Notes on the sheet:
  //   STEUERWERK
  //   SSTEP
  //   START
  //   DATA
  //   RUN
  //   HALT
  //   DSTCMD
  //   SRCCMD
  //   DSTRDY
  //   SRCRDY
  //   DSTREG
  //   CLK
  //   RST
  //   SRCREG
  //   HALT alt
  //   nHALT
  //   HALT ↑
  //   HALTP
  //   RUN alt
  //   nRUN
  //   RUN ↑
  //   RUNP
  //   START alt
  //   nSTART
  //   START ↑
  //   STARTP
  //   SSTEP alt
  //   nSSTEP
  //   SSTEP ↑
  //   SSTEPP
  //   ADRZÄHLER
  //   NEXT
  //   UPC
  //   Diodenmatrix 64×12
  //   contents of rom_1 (hex, n*v repeats v):
  //   113 4e7 6b 3c0 340 140 186 80 1c2 c0 186 41f 0 1c2 300 141 200 1c2 5c1 380 113 40 240 100 180 877
  //   643 280 8ff 70b 2ca 1c2 1 1c6 6c1 2fa 781 1 1 1 1 1 1 1 1 1 1 1 1 1 1 1 1 1 1 1 1 1 1 1 1 1 1 1
  //   W
  //   ROM 00..11
  //   AT
  //   CT
  //   CODE
  //   CHK
  //   TEST
  //   ROM 02..05
  //   CMD
  //   HLTFF
  //   DSTFF
  //   STRTFF
  //   SSTPFF
  //   CHKSEL
  //   SIG
  //   CHECK
  //   TRUE
  //   nTRUE
  //   nCT
  //   nAT
  //   jc
  //   ADR (Sprung)
  //   JUMP
  //   INCTST warten
  //   HOLD
  //   INC
  //   UPC1
  //   m1
  //   nächste Adresse
  //   CMDDEC 74154
  //   C8
  //   C9
  //   C10
  //   C11
  //   C12
  //   C13
  //   C14
  //   C15
  //   C0
  //   C1
  //   C2
  //   C3
  //   C4
  //   C5
  //   C6
  //   C7
  //   ldSB
  //   dSB
  //   SRCBUF
  //   DATBUF
  //   SRCBUF
  //   DATBUF
  //   ldSO
  //   soSel
  //   dSO
  //   SOURCE
  //   SRC
  //   ldDB
  //   DSTBUF
  //   dDB
  //   DST
  //   SRCENB
  //   SRCENB
  //   DSTENB
  //   DSTENB
  //   DSTFF
  //   STRTFF
  //   SSTPFF
  //   HLTFF
endmodule

module SPEICHER (
  input  [11:0] SRC,
  input  [11:0] DST,
  input  SRCENB,
  input  DSTENB,
  input  [11:0] DATA,
  input  CLK,
  input  RST,
  output [11:0] DOUT,
  output SRDY,
  output DRDY
);

  wire devsel_1_end, devsel_1_pls, devsel_1_sel, devsel_2_end, devsel_2_pls, devsel_2_sel, nor_1_out,
       nor_2_out;
  wire [9:0] multiplexer_1_out;
  wire [11:0] ram_1_data, register_1_q;

  nor nor_1 (nor_1_out, SRC[10], SRC[11]);
  nor nor_2 (nor_2_out, DST[10], DST[11]);
  DEVSEL devsel_1 (
    .MATCH(nor_1_out), .ENB(SRCENB), .CLK(CLK), .RST(RST), .SEL(devsel_1_sel), .RDY(SRDY),
    .PLS(devsel_1_pls), .END(devsel_1_end));
  DEVSEL devsel_2 (
    .MATCH(nor_2_out), .ENB(DSTENB), .CLK(CLK), .RST(RST), .SEL(devsel_2_sel), .RDY(DRDY),
    .PLS(devsel_2_pls), .END(devsel_2_end));
  Multiplexer #(.select(1), .width(10), .enable("false")) multiplexer_1 (
    .in0(SRC[9:0]), .in1(DST[9:0]), .out(multiplexer_1_out), .sel(devsel_2_sel));
  RAM #(.addrWidth(10), .dataWidth(12), .bus("separate")) ram_1 (
    .addr(multiplexer_1_out), .din(DATA), .data(ram_1_data), .str(devsel_2_pls), .clk(CLK));  // open: sel, ld, clr
  Register #(.width(12)) register_1 (.D(ram_1_data), .en(devsel_1_pls), .Q(register_1_q), .clk(CLK));  // open: clr
  Multiplexer #(.select(1), .width(12), .enable("false")) multiplexer_2 (
    .in0({12{1'b0}}), .in1(register_1_q), .out(DOUT), .sel(devsel_1_sel));

  // Notes on the sheet:
  //   SPEICHER
  //   CLK
  //   RST
  //   SRC
  //   DST
  //   SRCENB
  //   DSTENB
  //   DATA
  //   SRC
  //   s11
  //   s10
  //   sA
  //   SRC<2000
  //   mS
  //   DST
  //   d11
  //   d10
  //   dA
  //   DST<2000
  //   mD
  //   DEVSEL SRC
  //   plsS
  //   SRDY
  //   selS
  //   DEVSEL DST
  //   plsD
  //   DRDY
  //   Adresse
  //   selD
  //   ADR
  //   RAM 1k × 12
  //   contents of ram_1 (hex, n*v repeats v):
  //   ff2 fec ff2 2e ff2 2f ff2 30 31 ff2 32 ff3 33 ff1 ff3 2e 30 ff3 2f ff2 ff4 fc6 ff3 30 ff2 2f ff2 fec
  //   ff5 ff6 ff6 ff2 34 fc6 ff2 ffe 35 ffe fff 0 2e ff2 ff5 ff3 36 ffe 0 0 0 b07 99c 972 24 28 c 0 0 0 0
  //   0 0 0 0 0 4b ff4 4a ff0 ff3 4c ff2 4d fff 0 979 cdc 0 0 0 0 0 0 0 0 0 0 0 0 0 0 0 0 0 0 0 0 0 0 0 0
  //   0 0 0 0 0 0 0 0 0 0 0 0 0 0 0 0 0 0 0 0 0 0 0 0 0 0 0 0 0 0 0 0 0 0 0 0 0 0 0 0 0 0 0 0 0 0 0 0 0 0
  //   0 0 0 0 0 0 0 0 0 0 0 0 0 0 0 0 0 0 0 0 0 0 0 0 0 0 0 0 0 0 0 0 0 0 0 0 0 0 0 0 0 0 0 0 0 0 0 0 0 0
  //   0 0 0 0 0 0 0 0 0 0 0 0 0 0 0 0 0 0 0 0 0 0 0 0 0 0 0 0 0 0 0 0 0 0 0 0 0 0 0 0 0 0 0 0 0 0 0 0 0 0
  //   0 0 0 0 0 0 0 0 0 0 0 0 0 0 0 0 0 0 0 0 0 0 0 0 0 0 0 0 0 0 0 0 0 0 0 0 0 0 0 0 0 0 0 0 0 0 0 0 0 0
  //   0 0 0 0 0 0 0 0 0 0 0 0 0 0 0 0 0 0 0 0 0 0 0 0 0 0 0 0 0 0 0 0 0 0 0 0 0 0 0 0 0 0 0 0 0 0 0 0 0 0
  //   0 0 0 0 0 0 0 0 0 0 0 0 0 0 0 0 0 0 0 0 0 0 0 0 0 0 0 0 0 0 0 0 0 0 0 0 0 0 0 0 0 0 0 0 0 0 0 0 0 0
  //   0 0 0 0 0 0 0 0 0 0 0 0 0 0 0 0 0 0 0 0 0 0 0 0 0 0 0 0 0 0 0 0 0 0 0 0 0 0 0 0 0 0 0 0 0 0 0 0 0 0
  //   0 0 0 0 0 0 0 0 0 0 0 0 0 0 0 0 0 0 0 0 0 0 0 0 0 0 0 0 0 0 0 0 0 0 0 0 0 0 0 0 0 0 0 0 0 0 0 0 0 0
  //   0 0 0 0 0 0 0 0 0 0 0 0 0 0 0 0 0 0 0 0 0 0 0 0 0 0 0 0 0 0 0 0 0 0 0 0 0 0 0 0 0 0 0 0 0 0 0 0 0 0
  //   0 0 0 0 0 0 0 0 0 0 0 0 0 0 0 0 0 0 0 0 0 0 0 0 0 0 0 0 0 0 0 0 0 0 0 0 0 0 0 0 0 0 0 0 0 0 0 0 0 0
  //   0 0 0 0 0 0 0 0 0 0 0 0 0 0 0 0 0 0 0 0 0 0 0 0 0 0 0 0 0 0 0 0 0 0 0 0 0 0 0 0 0 0 0 0 0 0 0 0 0 0
  //   0 0 0 0 0 0 0 0 0 0 0 0 0 0 0 0 0 0 0 0 0 0 0 0 0 0 0 0 0 0 0 0 0 0 0 0 0 0 0 0 0 0 0 0 0 0 0 0 0 0
  //   0 0 0 0 0 0 0 0 0 0 0 0 0 0 0 0 0 0 0 0 0 0 0 0 0 0 0 0 0 0 0 0 0 0 0 0 0 0 0 0 0 0 0 0 0 0 0 0 0 0
  //   0 0 0 0 0 0 0 0 0 0 0 0 0 0 0 0 0 0 0 0 0 0 0 0 0 0 0 0 0 0 0 0 0 0 0 0 0 0 0 0 0 0 0 0 0 0 0 0 0 0
  //   0 0 0 0 0 0 0 0 0 0 0 0 0 0 0 0 0 0 0 0 0 0 0 0 0 0 0 0 0 0 0 0 0 0 0 0 0 0 0 0 0 0 0 0 0 0 0 0 0 0
  //   0 0 0 0 0 0 0 0 0 0 0 0 0 0 0 0 0 0 0 0 0 0 0 0 0 0 0 0 0 0 0 0 0 0 0 0 0 0 0 0 0 0 0 0 0 0 0 0 0 0
  //   0 0 0 0 0 0 0 0 0 0 0 0 0 0 0 0 0 0 0 0 0 0 0 0 0 0 0 0 0 0 0 0 0 0 0 0 0 0 0 0 0 0 0 0 0 0 0 0 0 0
  //   0 0 0 0 0 0 0 0 0 0 0 0 0 0 0 0 0 0 0 0 0 0 0 0 0 0 0 0 0 0 0 0 0 0 0 0 0 0 0 0 0 0 0 0 0 0 0 0 0 0
  //   0 0 0 0 0 0 0 0 0 0 0 0 0 0 0 0 0 0 0 0 0 0 0 0
  //   RD
  //   MEMBUF
  //   MB
  //   auf DATA
  //   DOUT
endmodule

module PROGRAMMZAEHLER (
  input  [11:0] SRC,
  input  [11:0] DST,
  input  SRCENB,
  input  DSTENB,
  input  [11:0] DATA,
  input  CLK,
  input  RST,
  output [11:0] DOUT,
  output SRDY,
  output DRDY,
  output [11:0] PC
);

  wire adder_1_cout, adreq_1_eq, adreq_2_eq, devsel_1_end, devsel_1_pls, devsel_1_sel, devsel_2_end,
       devsel_2_pls, devsel_2_sel, or_1_out;
  wire [11:0] adder_1_out, multiplexer_1_out;

  ADREQ adreq_1 (.K(12'hffe), .A(SRC), .EQ(adreq_1_eq));
  ADREQ adreq_2 (.K(12'hffe), .A(DST), .EQ(adreq_2_eq));
  DEVSEL devsel_1 (
    .MATCH(adreq_1_eq), .ENB(SRCENB), .CLK(CLK), .RST(RST), .SEL(devsel_1_sel), .RDY(SRDY),
    .PLS(devsel_1_pls), .END(devsel_1_end));
  DEVSEL devsel_2 (
    .MATCH(adreq_2_eq), .ENB(DSTENB), .CLK(CLK), .RST(RST), .SEL(devsel_2_sel), .RDY(DRDY),
    .PLS(devsel_2_pls), .END(devsel_2_end));
  Adder #(.width(12)) adder_1 (.a(PC), .b({12{1'b0}}), .out(adder_1_out), .cin(1'b1), .cout(adder_1_cout));
  Multiplexer #(.select(1), .width(12), .enable("false")) multiplexer_1 (
    .in0(adder_1_out), .in1(DATA), .out(multiplexer_1_out), .sel(devsel_2_pls));
  or or_1 (or_1_out, devsel_2_pls, devsel_1_end);
  Register #(.width(12)) register_1 (.D(multiplexer_1_out), .en(or_1_out), .Q(PC), .clk(CLK));  // open: clr
  Multiplexer #(.select(1), .width(12), .enable("false")) multiplexer_2 (
    .in0({12{1'b0}}), .in1(PC), .out(DOUT), .sel(devsel_1_sel));

  // Notes on the sheet:
  //   PROGRAMMZAEHLER
  //   CLK
  //   RST
  //   SRC
  //   DST
  //   SRCENB
  //   DSTENB
  //   DATA
  //   = 7776 ?
  //   mS
  //   = 7776 ?
  //   mD
  //   DEVSEL SRC
  //   endS
  //   SRDY
  //   selS
  //   DEVSEL DST
  //   plsD
  //   DRDY
  //   PC
  //   +1
  //   PC1
  //   Laden/Zählen
  //   dPC
  //   ldPC
  //   PC
  //   auf DATA
  //   DOUT
endmodule

module SWITCHREG (
  input  [11:0] SRC,
  input  [11:0] DST,
  input  SRCENB,
  input  DSTENB,
  input  [11:0] DATA,
  input  [11:0] SR,
  input  CLK,
  input  RST,
  output [11:0] DOUT,
  output SRDY,
  output DRDY,
  output [11:0] SRANZ
);

  wire adreq_1_eq, adreq_2_eq, devsel_1_end, devsel_1_pls, devsel_1_sel, devsel_2_end, devsel_2_pls,
       devsel_2_sel;

  ADREQ adreq_1 (.K(12'hffc), .A(SRC), .EQ(adreq_1_eq));
  ADREQ adreq_2 (.K(12'hffc), .A(DST), .EQ(adreq_2_eq));
  DEVSEL devsel_1 (
    .MATCH(adreq_1_eq), .ENB(SRCENB), .CLK(CLK), .RST(RST), .SEL(devsel_1_sel), .RDY(SRDY),
    .PLS(devsel_1_pls), .END(devsel_1_end));
  DEVSEL devsel_2 (
    .MATCH(adreq_2_eq), .ENB(DSTENB), .CLK(CLK), .RST(RST), .SEL(devsel_2_sel), .RDY(DRDY),
    .PLS(devsel_2_pls), .END(devsel_2_end));
  Register #(.width(12)) register_1 (.D(DATA), .en(devsel_2_pls), .Q(SRANZ), .clk(CLK));  // open: clr
  Multiplexer #(.select(1), .width(12), .enable("false")) multiplexer_1 (
    .in0({12{1'b0}}), .in1(SR), .out(DOUT), .sel(devsel_1_sel));

  // Notes on the sheet:
  //   SWITCHREG
  //   CLK
  //   RST
  //   SRC
  //   DST
  //   SRCENB
  //   DSTENB
  //   DATA
  //   SR
  //   = 7774 ?
  //   mS
  //   = 7774 ?
  //   mD
  //   DEVSEL SRC
  //   SRDY
  //   selS
  //   DEVSEL DST
  //   plsD
  //   DRDY
  //   SR-Anzeige
  //   ANZ
  //   auf DATA
  //   DOUT
endmodule

module RECHENWERK (
  input  [11:0] SRC,
  input  [11:0] DST,
  input  SRCENB,
  input  DSTENB,
  input  [11:0] DATA,
  input  CLK,
  input  RST,
  output [11:0] DOUT,
  output SRDY,
  output DRDY,
  output [23:0] RR,
  output [11:0] R2,
  output [11:0] R3,
  output CO,
  output GL
);

  wire adder_1_cout, adder_2_cout, adreq_1_eq, adreq_2_eq, adreq_3_eq, adreq_4_eq, adreq_5_eq, adreq_6_eq,
       adreq_7_eq, adreq_8_eq, adreq_9_eq, adreq_10_eq, adreq_11_eq, adreq_12_eq, adreq_13_eq,
       alu_6x74181_1_co, alu_6x74181_1_eq, and_1_out, and_2_out, and_3_out, and_4_out, and_5_out, and_6_out,
       and_11_out, and_12_out, and_13_out, and_14_out, and_15_out, and_16_out, d_ff_1_q, d_ff_1_qn,
       d_ff_2_qn, d_ff_3_qn, devsel_1_end, devsel_1_pls, devsel_1_sel, devsel_2_end, devsel_2_pls,
       devsel_2_rdy, devsel_2_sel, j_k_ff_1_q, j_k_ff_1_qn, j_k_ff_2_q, j_k_ff_2_qn, multiplexer_8_out,
       nand_1_out, not_2_out, or_2_out, or_3_out, or_4_out, or_5_out, or_6_out, or_9_out, or_10_out,
       or_11_out, or_12_out;
  wire [0:0] and_10_out, multiplexer_9_out;
  wire [1:0] or_7_out;
  wire [2:0] or_13_out;
  wire [3:0] adder_1_out, adder_2_out, multiplexer_1_out, multiplexer_2_out, not_1_out, register_1_q,
       xnor_1_out;
  wire [5:0] multiplexer_3_out, multiplexer_4_out, multiplexer_5_out;
  wire [5:4] and_8_out;
  wire [11:0] multiplexer_10_out, multiplexer_11_out, or_1_out;
  wire [23:0] alu_6x74181_1_f, multiplexer_6_out, multiplexer_7_out;

  assign or_1_out = DST | 12'h3f;  // OR_Gate or_1, 12 bits wide
  ADREQ adreq_1 (.K({12{1'b1}}), .A(or_1_out), .EQ(adreq_1_eq));
  nand nand_1 (nand_1_out, DST[4], DST[5]);
  and and_1 (and_1_out, adreq_1_eq, nand_1_out);
  ADREQ adreq_2 (.K(12'hff0), .A(DST), .EQ(adreq_2_eq));
  ADREQ adreq_3 (.K(12'hff1), .A(DST), .EQ(adreq_3_eq));
  ADREQ adreq_4 (.K(12'hff2), .A(DST), .EQ(adreq_4_eq));
  ADREQ adreq_5 (.K(12'hff3), .A(DST), .EQ(adreq_5_eq));
  ADREQ adreq_6 (.K(12'hff4), .A(DST), .EQ(adreq_6_eq));
  ADREQ adreq_7 (.K(12'hff6), .A(DST), .EQ(adreq_7_eq));
  ADREQ adreq_8 (.K(12'hff2), .A(SRC), .EQ(adreq_8_eq));
  ADREQ adreq_9 (.K(12'hff3), .A(SRC), .EQ(adreq_9_eq));
  ADREQ adreq_10 (.K(12'hff4), .A(SRC), .EQ(adreq_10_eq));
  ADREQ adreq_11 (.K(12'hff5), .A(SRC), .EQ(adreq_11_eq));
  ADREQ adreq_12 (.K(12'hff6), .A(SRC), .EQ(adreq_12_eq));
  ADREQ adreq_13 (.K(12'hff7), .A(SRC), .EQ(adreq_13_eq));
  or or_2 (or_2_out, and_1_out, adreq_2_eq, adreq_3_eq, adreq_4_eq, adreq_5_eq, adreq_6_eq, adreq_7_eq);
  or or_3 (or_3_out, adreq_8_eq, adreq_9_eq, adreq_10_eq, adreq_11_eq, adreq_12_eq, adreq_13_eq);
  DEVSEL devsel_1 (
    .MATCH(or_3_out), .ENB(SRCENB), .CLK(CLK), .RST(RST), .SEL(devsel_1_sel), .RDY(SRDY), .PLS(devsel_1_pls),
    .END(devsel_1_end));
  DEVSEL devsel_2 (
    .MATCH(or_2_out), .ENB(DSTENB), .CLK(CLK), .RST(RST), .SEL(devsel_2_sel), .RDY(devsel_2_rdy),
    .PLS(devsel_2_pls), .END(devsel_2_end));
  or or_4 (or_4_out, adreq_2_eq, adreq_3_eq);
  and and_2 (and_2_out, devsel_2_pls, or_4_out);
  and and_3 (and_3_out, devsel_2_pls, adreq_2_eq);
  J_K_Flip_Flop j_k_ff_1 (
    .J(and_2_out), .clk(CLK), .K(and_6_out), .Q(j_k_ff_1_q), .Qn(j_k_ff_1_qn), .reset(RST));  // open: preset, en
  J_K_Flip_Flop j_k_ff_2 (
    .J(j_k_ff_1_q), .clk(CLK), .K(j_k_ff_1_q), .Q(j_k_ff_2_q), .Qn(j_k_ff_2_qn), .reset(RST));  // open: preset, en
  and and_4 (and_4_out, j_k_ff_1_q, j_k_ff_2_qn);
  and and_5 (and_5_out, j_k_ff_1_q, j_k_ff_2_q);
  Adder #(.width(4)) adder_1 (.a(register_1_q), .b(4'b0000), .out(adder_1_out), .cin(1'b1), .cout(adder_1_cout));
  Multiplexer #(.select(1), .width(4), .enable("false")) multiplexer_1 (
    .in0(adder_1_out), .in1(4'b0000), .out(multiplexer_1_out), .sel(and_2_out));
  or or_5 (or_5_out, and_2_out, and_5_out);
  Register #(.width(4)) register_1 (.D(multiplexer_1_out), .en(or_5_out), .Q(register_1_q), .clk(CLK), .clr(RST));
  assign xnor_1_out = ~(register_1_q ^ 4'b1011);  // XNOR_Gate xnor_1, 4 bits wide
  Adder #(.width(4)) adder_2 (.a(xnor_1_out), .b(4'b0000), .out(adder_2_out), .cin(1'b1), .cout(adder_2_cout));
  and and_6 (and_6_out, and_5_out, adder_2_cout);
  and and_7 (DRDY, devsel_2_rdy, j_k_ff_1_qn);
  assign not_1_out = ~DST[3:0];  // NOT_Gate not_1, 4 bits wide
  Multiplexer #(.select(1), .width(4), .enable("false")) multiplexer_2 (
    .in0(not_1_out), .in1(4'b0110), .out(multiplexer_2_out), .sel(adreq_7_eq));
  not not_2 (not_2_out, adreq_7_eq);
  and and_8 (and_8_out[4], DST[4], not_2_out);
  and and_9 (and_8_out[5], DST[5], not_2_out);
  Multiplexer #(.select(1), .width(6), .enable("false")) multiplexer_3 (
    .in0(6'b001001), .in1(6'b010110), .out(multiplexer_3_out), .sel(adreq_3_eq));
  Multiplexer #(.select(1), .width(6), .enable("false")) multiplexer_4 (
    .in0(6'b001100), .in1(multiplexer_3_out), .out(multiplexer_4_out), .sel(j_k_ff_2_q));
  Multiplexer #(.select(1), .width(6), .enable("false")) multiplexer_5 (
    .in0({and_8_out, multiplexer_2_out}), .in1(multiplexer_4_out), .out(multiplexer_5_out), .sel(j_k_ff_1_q));
  Multiplexer #(.select(1), .width(24), .enable("false")) multiplexer_6 (
    .in0({{12{1'b0}}, DATA}), .in1({DATA, {12{1'b0}}}), .out(multiplexer_6_out), .sel(adreq_3_eq));
  ALU_6x74181 alu_6x74181_1 (
    .A(RR), .B(multiplexer_6_out), .S(multiplexer_5_out[3:0]), .M(multiplexer_5_out[5]),
    .CN(multiplexer_5_out[4]), .F(alu_6x74181_1_f), .CO(alu_6x74181_1_co), .EQ(alu_6x74181_1_eq));
  D_Flip_Flop d_ff_1 (
    .clk(CLK), .D(alu_6x74181_1_co), .Q(d_ff_1_q), .Qn(d_ff_1_qn), .en(and_4_out));  // open: preset, reset
  or or_6 (or_6_out, d_ff_1_q, alu_6x74181_1_co);
  and and_10 (and_10_out[0], d_ff_1_q, alu_6x74181_1_co);
  or or_7 (or_7_out[0], adreq_4_eq, and_3_out);
  or or_8 (or_7_out[1], adreq_5_eq, and_3_out);
  Multiplexer #(.select(2), .width(24), .enable("false")) multiplexer_7 (
    .in0(alu_6x74181_1_f), .in1({RR[23:12], DATA}), .in2({DATA, RR[11:0]}), .in3({24{1'b0}}),
    .out(multiplexer_7_out), .sel(or_7_out));
  or or_9 (or_9_out, and_1_out, adreq_4_eq, adreq_5_eq);
  and and_11 (and_11_out, devsel_2_pls, or_9_out);
  Multiplexer #(.select(1), .width(1), .enable("false")) multiplexer_8 (
    .in0(R2[11]), .in1(or_6_out), .out(multiplexer_8_out), .sel(adreq_3_eq));
  and and_12 (and_12_out, and_5_out, multiplexer_8_out);
  or or_10 (or_10_out, and_11_out, and_3_out, and_4_out, and_12_out);
  Register #(.width(24)) register_2 (.D(multiplexer_7_out), .en(or_10_out), .Q(RR), .clk(CLK));  // open: clr
  Multiplexer #(.select(1), .width(1), .enable("false")) multiplexer_9 (
    .in0(R2[11]), .in1(or_6_out), .out(multiplexer_9_out[0]), .sel(adreq_3_eq));
  and and_13 (and_13_out, devsel_2_pls, adreq_6_eq);
  Multiplexer #(.select(1), .width(12), .enable("false")) multiplexer_10 (
    .in0({R2[10:0], multiplexer_9_out[0]}), .in1(DATA), .out(multiplexer_10_out), .sel(and_13_out));
  or or_11 (or_11_out, and_13_out, and_5_out);
  Register #(.width(12)) register_3 (.D(multiplexer_10_out), .en(or_11_out), .Q(R2), .clk(CLK));  // open: clr
  and and_14 (and_14_out, and_5_out, adreq_3_eq);
  Register #(.width(12)) register_4 (.D({R3[10:0], and_10_out[0]}), .en(and_14_out), .Q(R3), .clk(CLK));  // open: clr
  or or_12 (or_12_out, and_1_out, adreq_7_eq);
  and and_15 (and_15_out, devsel_2_pls, or_12_out);
  and and_16 (and_16_out, devsel_2_pls, adreq_7_eq);
  D_Flip_Flop d_ff_2 (.clk(CLK), .D(alu_6x74181_1_co), .Q(CO), .Qn(d_ff_2_qn), .en(and_15_out));  // open: preset, reset
  D_Flip_Flop d_ff_3 (.clk(CLK), .D(alu_6x74181_1_eq), .Q(GL), .Qn(d_ff_3_qn), .en(and_16_out));  // open: preset, reset
  or or_13 (or_13_out[0], adreq_9_eq, adreq_12_eq, adreq_11_eq);
  or or_14 (or_13_out[1], adreq_13_eq, adreq_12_eq);
  or or_15 (or_13_out[2], adreq_10_eq, adreq_11_eq);
  Multiplexer #(.select(3), .width(12), .enable("false")) multiplexer_11 (
    .in0(RR[11:0]), .in1(RR[23:12]), .in2({{10{1'b0}}, CO, 1'b0}), .in3({{10{1'b0}}, GL, 1'b0}), .in4(R2),
    .in5(R3), .in6({12{1'b0}}), .in7({12{1'b0}}), .out(multiplexer_11_out), .sel(or_13_out));
  Multiplexer #(.select(1), .width(12), .enable("false")) multiplexer_12 (
    .in0({12{1'b0}}), .in1(multiplexer_11_out), .out(DOUT), .sel(devsel_1_sel));

  // Notes on the sheet:
  //   RECHENWERK
  //   CLK
  //   RST
  //   SRC
  //   DST
  //   SRCENB
  //   DSTENB
  //   DATA
  //   DST ∨ 0077
  //   dor
  //   DST=77xx ?
  //   hi77
  //   DST 00..05
  //   b5
  //   b4
  //   lo4
  //   nicht 776x
  //   n45
  //   ALU 7700-7757
  //   dALU
  //   = 7760 ?
  //   dVM
  //   = 7761 ?
  //   dDL
  //   = 7762 ?
  //   dR0
  //   = 7763 ?
  //   dR1
  //   = 7764 ?
  //   dR2
  //   = 7766 ?
  //   dGL
  //   = 7762 ?
  //   sR0
  //   = 7763 ?
  //   sR1
  //   = 7764 ?
  //   sR2
  //   = 7765 ?
  //   sR3
  //   = 7766 ?
  //   sGL
  //   = 7767 ?
  //   sCO
  //   DST-Match
  //   mD
  //   SRC-Match
  //   mS
  //   DEVSEL SRC
  //   SRDY
  //   selS
  //   DEVSEL DST
  //   plsD
  //   rdyD
  //   dVD
  //   Start VD
  //   vdStart
  //   VM: RR:=0
  //   vmStart
  //   vdDone
  //   VDBUSY
  //   nBUSY
  //   BUSY
  //   OPAF (sonst SCHUIF)
  //   nPH
  //   PH
  //   SCHUIF
  //   vdShift
  //   OPAF
  //   vdOp
  //   CNT
  //   +1
  //   CNT1
  //   dCNT
  //   12-Teiler
  //   ldCNT
  //   = 11 ?
  //   c11x
  //   c11
  //   Ende VD
  //   DSTRDY erst nach VD
  //   DRDY
  //   S = ¬Bits
  //   nlo4
  //   GL: S=0110
  //   Sn
  //   ndGL
  //   Cn
  //   CNn
  //   M
  //   Mn
  //   ctlN
  //   OPAF: VM A+B / DL A−B
  //   ctlOp
  //   SCHUIF: A+A
  //   ctlVD
  //   ALU-Modus
  //   ctl
  //   M
  //   CN
  //   S
  //   Blo
  //   DATA unten
  //   Bhi
  //   DATA oben (DL)
  //   B-Eingang
  //   B24
  //   RR
  //   ALU (6 × 74181)
  //   aEQ
  //   aCO
  //   F
  //   SFCRY
  //   CS
  //   Bi (DL)
  //   bi
  //   Overflow
  //   RR → R0/R1
  //   ovf
  //   RRhi
  //   RRlo
  //   vR0
  //   R0 := DATA
  //   R1 := DATA
  //   vR1
  //   rs0
  //   rs1
  //   rrSel
  //   RR-Eingang
  //   dRR
  //   nrm
  //   ldN
  //   R2 → Bj
  //   R2
  //   R2b11
  //   R2lo
  //   addieren/subtr.?
  //   opc
  //   ldOp
  //   ldRR
  //   RR (R1:R0)
  //   R2 schieben
  //   r2in
  //   R2sh
  //   ldR2d
  //   dR2v
  //   ldR2
  //   R2
  //   R3
  //   R3lo
  //   R3 schieben
  //   R3sh
  //   ldR3
  //   R3
  //   coop
  //   ldCO
  //   ldGL
  //   CO
  //   CO
  //   GL
  //   CO → 0/2
  //   GL
  //   CO2
  //   GL → 0/2
  //   GL2
  //   q0
  //   q1
  //   q2
  //   srcSel
  //   SRC-Auswahl
  //   val
  //   auf DATA
  //   DOUT
endmodule

module HALT (
  input  [11:0] SRC,
  input  SRCENB,
  output HRST
);

  wire adreq_1_eq;

  ADREQ adreq_1 (.K({12{1'b1}}), .A(SRC), .EQ(adreq_1_eq));
  and and_1 (HRST, adreq_1_eq, SRCENB);

  // Notes on the sheet:
  //   HALT
  //   SRCENB
  //   SRC
  //   = 7777 ?
  //   m
  //   RESET
  //   R
endmodule

module ALU_6x74181 (
  input  [23:0] A,
  input  [23:0] B,
  input  [3:0] S,
  input  M,
  input  CN,
  output [23:0] F,
  output CO,
  output EQ
);

  wire [23:0] adder_1_out, adder_2_out, and_1_out, and_2_out, and_3_out, and_4_out, multiplexer_1_out,
       multiplexer_2_out, multiplexer_3_out, multiplexer_4_out, not_1_out, or_1_out, or_2_out, xnor_1_out;

  Multiplexer #(.select(1), .width(24), .enable("false")) multiplexer_1 (
    .in0({24{1'b0}}), .in1({24{1'b1}}), .out(multiplexer_1_out), .sel(S[0]));
  Multiplexer #(.select(1), .width(24), .enable("false")) multiplexer_2 (
    .in0({24{1'b0}}), .in1({24{1'b1}}), .out(multiplexer_2_out), .sel(S[1]));
  Multiplexer #(.select(1), .width(24), .enable("false")) multiplexer_3 (
    .in0({24{1'b0}}), .in1({24{1'b1}}), .out(multiplexer_3_out), .sel(S[2]));
  Multiplexer #(.select(1), .width(24), .enable("false")) multiplexer_4 (
    .in0({24{1'b0}}), .in1({24{1'b1}}), .out(multiplexer_4_out), .sel(S[3]));
  assign not_1_out = ~B;  // NOT_Gate not_1, 24 bits wide
  assign and_1_out = multiplexer_1_out & B;  // AND_Gate and_1, 24 bits wide
  assign and_2_out = multiplexer_2_out & not_1_out;  // AND_Gate and_2, 24 bits wide
  assign or_1_out = A | and_1_out | and_2_out;  // OR_Gate or_1, 24 bits wide
  assign and_3_out = multiplexer_3_out & A & not_1_out;  // AND_Gate and_3, 24 bits wide
  assign and_4_out = multiplexer_4_out & A & B;  // AND_Gate and_4, 24 bits wide
  assign or_2_out = and_3_out | and_4_out;  // OR_Gate or_2, 24 bits wide
  Adder #(.width(24)) adder_1 (.a(or_1_out), .b(or_2_out), .out(adder_1_out), .cin(CN), .cout(CO));
  assign xnor_1_out = ~(or_1_out ^ or_2_out);  // XNOR_Gate xnor_1, 24 bits wide
  Multiplexer #(.select(1), .width(24), .enable("false")) multiplexer_5 (
    .in0(adder_1_out), .in1(xnor_1_out), .out(F), .sel(M));
  Adder #(.width(24)) adder_2 (.a(F), .b({24{1'b0}}), .out(adder_2_out), .cin(1'b1), .cout(EQ));

  // Notes on the sheet:
  //   ALU_6x74181
  //   CN
  //   M
  //   S
  //   B
  //   A
  //   S3..S0
  //   s3
  //   s2
  //   s1
  //   s0
  //   S0
  //   S0x
  //   S1
  //   S1x
  //   S2
  //   S2x
  //   S3
  //   S3x
  //   B quer
  //   S0·B
  //   nB
  //   t1
  //   S1·B quer
  //   t2
  //   X
  //   X
  //   S2·A·B quer
  //   t3
  //   S3·A·B
  //   t4
  //   Y
  //   Y
  //   arithm. X+Y+Cn
  //   CO
  //   Fa
  //   logisch
  //   Fl
  //   M
  //   F
  //   A=B (F alle 1)
  //   EQ
endmodule

module DEVSEL (
  input  MATCH,
  input  ENB,
  input  CLK,
  input  RST,
  output SEL,
  output RDY,
  output PLS,
  output END
);

  wire d_ff_1_qn, not_1_out;

  and and_1 (SEL, MATCH, ENB);
  D_Flip_Flop d_ff_1 (.clk(CLK), .D(SEL), .Q(RDY), .Qn(d_ff_1_qn), .reset(RST));  // open: preset, en
  not not_1 (not_1_out, SEL);
  and and_2 (PLS, SEL, d_ff_1_qn);
  and and_3 (END, not_1_out, RDY);

  // Notes on the sheet:
  //   DEVSEL
  //   RST
  //   CLK
  //   ENB
  //   MATCH
  //   SEL
  //   SEL
  //   FNKFF
  //   nQ
  //   Q
  //   nSEL
  //   FNKPLS
  //   PLS
  //   Ende
  //   END
endmodule

module ADREQ (
  input  [11:0] K,
  input  [11:0] A,
  output EQ
);

  wire [11:0] adder_1_out, xnor_1_out;

  assign xnor_1_out = ~(A ^ K);  // XNOR_Gate xnor_1, 12 bits wide
  Adder #(.width(12)) adder_1 (.a(xnor_1_out), .b({12{1'b0}}), .out(adder_1_out), .cin(1'b1), .cout(EQ));

  // Notes on the sheet:
  //   ADREQ
  //   A
  //   K
  //   Vergleich
  //   x
  //   alle 1?
  //   EQ
endmodule
