// Logisim project intel4004.circ as structural Verilog: 23 circuits, main circuit System_4004
module Buendel_6 (
  input  b0,
  input  b1,
  input  b2,
  input  b3,
  input  b4,
  input  b5,
  output [5:0] bus
);


  assign bus = {b5, b4, b3, b2, b1, b0};
endmodule

module Buendel_2 (
  input  b0,
  input  b1,
  output [1:0] bus
);


  assign bus = {b1, b0};
endmodule

module Buendel_8 (
  input  b0,
  input  b1,
  input  b2,
  input  b3,
  input  b4,
  input  b5,
  input  b6,
  input  b7,
  output [7:0] bus
);


  assign bus = {b7, b6, b5, b4, b3, b2, b1, b0};
endmodule

module Buendel_3 (
  input  b0,
  input  b1,
  input  b2,
  output [2:0] bus
);


  assign bus = {b2, b1, b0};
endmodule

module Buendel_12 (
  input  b0,
  input  b1,
  input  b2,
  input  b3,
  input  b4,
  input  b5,
  input  b6,
  input  b7,
  input  b8,
  input  b9,
  input  b10,
  input  b11,
  output [11:0] bus
);


  assign bus = {b11, b10, b9, b8, b7, b6, b5, b4, b3, b2, b1, b0};
endmodule

module Buendel_4 (
  input  b0,
  input  b1,
  input  b2,
  input  b3,
  output [3:0] bus
);


  assign bus = {b3, b2, b1, b0};
endmodule

module Dekoder_3zu8 (
  input  [2:0] A,
  input  EN,
  output Y0,
  output Y1,
  output Y2,
  output Y7,
  output Y3,
  output Y4,
  output Y5,
  output Y6
);

  wire not_1_out, not_2_out, not_3_out;

  not not_1 (not_1_out, A[2]);
  not not_2 (not_2_out, A[1]);
  not not_3 (not_3_out, A[0]);
  and and_1 (Y7, EN, A[0], A[1], A[2]);
  and and_2 (Y0, EN, not_3_out, not_2_out, not_1_out);
  and and_3 (Y1, EN, A[0], not_2_out, not_1_out);
  and and_4 (Y2, EN, not_3_out, A[1], not_1_out);
  and and_5 (Y3, EN, A[0], A[1], not_1_out);
  and and_6 (Y4, EN, not_3_out, not_2_out, A[2]);
  and and_7 (Y5, EN, A[0], not_2_out, A[2]);
  and and_8 (Y6, EN, not_3_out, A[1], A[2]);

  // Notes on the sheet:
  //   Dekoder 3 auf 8: Y[k] = EN und (A == k). Ersetzt den Demultiplexer (im Web-Simulator erst ab 3 Ausgaengen fehlerhaft).
endmodule

module Dekoder_2zu4 (
  input  [1:0] A,
  input  EN,
  output Y0,
  output Y1,
  output Y3,
  output Y2
);

  wire not_1_out, not_2_out;

  not not_1 (not_1_out, A[1]);
  not not_2 (not_2_out, A[0]);
  and and_1 (Y3, EN, A[0], A[1]);
  and and_2 (Y0, EN, not_2_out, not_1_out);
  and and_3 (Y1, EN, A[0], not_1_out);
  and and_4 (Y2, EN, not_2_out, A[1]);

  // Notes on the sheet:
  //   Dekoder 2 auf 4: Y[k] = EN und (A == k). Ersetzt den Demultiplexer (im Web-Simulator erst ab 3 Ausgaengen fehlerhaft).
endmodule

module ALU (
  input  [2:0] BS,
  input  [3:0] B,
  input  [1:0] CS,
  input  [3:0] A,
  input  [2:0] COS,
  input  CY,
  input  [2:0] RS,
  output COUT,
  output [3:0] RES
);

  wire adder_1_cout, and_1_out, multiplexer_1_out, not_2_out, or_1_out, or_2_out, or_3_out;
  wire [3:0] adder_1_out, buendel_4_1_bus, buendel_4_2_bus, buendel_4_3_bus, buendel_4_4_bus,
       buendel_4_5_bus, KBP_Tabelle_data, multiplexer_2_out, not_1_out, not_3_out;

  assign not_1_out = ~B;  // NOT_Gate not_1, 4 bits wide
  not not_2 (not_2_out, CY);
  assign not_3_out = ~A;  // NOT_Gate not_3, 4 bits wide
  Buendel_4 buendel_4_1 (.b0(CY), .b1(1'b0), .b2(1'b0), .b3(1'b0), .bus(buendel_4_1_bus));
  ROM #(.addrWidth(4), .dataWidth(4)) KBP_Tabelle (.addr(A), .data(KBP_Tabelle_data));  // open: sel
  or or_1 (or_1_out, A[2], A[1]);
  Multiplexer #(.select(2), .enable("false")) multiplexer_1 (
    .in0(CY), .in1(not_2_out), .in2(1'b0), .in3(1'b1), .out(multiplexer_1_out), .sel(CS));
  Buendel_4 buendel_4_2 (.b0(CY), .b1(A[0]), .b2(A[1]), .b3(A[2]), .bus(buendel_4_2_bus));
  Buendel_4 buendel_4_3 (.b0(A[1]), .b1(A[2]), .b2(A[3]), .b3(CY), .bus(buendel_4_3_bus));
  Buendel_4 buendel_4_4 (.b0(not_2_out), .b1(CY), .b2(1'b0), .b3(1'b1), .bus(buendel_4_4_bus));
  and and_1 (and_1_out, A[3], or_1_out);
  or or_2 (or_2_out, and_1_out, CY);
  Buendel_4 buendel_4_5 (.b0(1'b0), .b1(or_2_out), .b2(or_2_out), .b3(1'b0), .bus(buendel_4_5_bus));
  Multiplexer #(.select(3), .enable("false"), .width(4)) multiplexer_2 (
    .in0(B), .in1(not_1_out), .in2(4'b0000), .in3(4'b1111), .in4(buendel_4_5_bus), .in5(4'b0000),
    .in6(4'b0000), .in7(4'b0000), .out(multiplexer_2_out), .sel(BS));
  Adder #(.width(4)) adder_1 (
    .a(A), .b(multiplexer_2_out), .out(adder_1_out), .cin(multiplexer_1_out), .cout(adder_1_cout));
  or or_3 (or_3_out, CY, adder_1_cout);
  Multiplexer #(.select(3), .enable("false"), .width(4)) multiplexer_3 (
    .in0(adder_1_out), .in1(B), .in2(not_3_out), .in3(buendel_4_2_bus), .in4(buendel_4_3_bus),
    .in5(buendel_4_1_bus), .in6(buendel_4_4_bus), .in7(KBP_Tabelle_data), .out(RES), .sel(RS));
  Multiplexer #(.select(3), .enable("false")) multiplexer_4 (
    .in0(adder_1_cout), .in1(A[3]), .in2(A[0]), .in3(1'b0), .in4(1'b1), .in5(not_2_out), .in6(or_3_out),
    .in7(CY), .out(COUT), .sel(COS));

  // Notes on the sheet:
  //   ALU: ein 4-Bit-Addierer mit waehlbarem Operanden (BS) und Uebertrag (CS), Ergebnis-Mux (RS), Carry-Mux (COS).
  //   SUB/SBM = A + ~B + ~CY, DAC = A + F, IAC = A + 0 + 1, DAA addiert 6 wenn A>9 oder CY.
  //   Buendel 4
  //   b0
  //   b1
  //   bus
  //   b2
  //   b3
  //   contents of KBP_Tabelle (hex, n*v repeats v):
  //   0 1 2 f 3 f f f 4 7*f
  //   Buendel 4
  //   b0
  //   b1
  //   bus
  //   b2
  //   b3
  //   Buendel 4
  //   b0
  //   b1
  //   bus
  //   b2
  //   b3
  //   Buendel 4
  //   b0
  //   b1
  //   bus
  //   b2
  //   b3
  //   Buendel 4
  //   b0
  //   b1
  //   b2
  //   b3
  //   bus
endmodule

module Taktgeber (
  input  CLK,
  output SYNC,
  output [2:0] PH
);

  wire [2:0] adder_1_out;

  Register #(.width(3)) Phase (.D(adder_1_out), .Q(PH), .clk(CLK));  // open: en, clr
  Adder #(.width(3)) adder_1 (.a(PH), .b(3'b001), .out(adder_1_out));  // open: cin, cout
  and and_1 (SYNC, PH[0], PH[1], PH[2]);

  // Notes on the sheet:
  //   Taktgeber: 3-Bit-Zaehler, eine Taktflanke pro Subzyklus. 0=A1 1=A2 2=A3 3=M1 4=M2 5=X1 6=X2 7=X3.
  //   SYNC ist in X3 aktiv; die Peripherie setzt damit ihren eigenen Phasenzaehler auf A1.
endmodule

module Befehlsregister (
  input  IRH_WE,
  input  IRL_WE,
  input  [3:0] D_EIN,
  input  O2H_WE,
  input  CLK,
  input  O2L_WE,
  input  C2_D,
  input  C2_WE,
  output [3:0] OPR,
  output [3:0] OPA,
  output [3:0] O2H,
  output [3:0] O2L,
  output C2
);

  Register #(.width(4)) u_OPR (.D(D_EIN), .en(IRH_WE), .Q(OPR), .clk(CLK));  // open: clr
  Register #(.width(4)) u_OPA (.D(D_EIN), .en(IRL_WE), .Q(OPA), .clk(CLK));  // open: clr
  Register #(.width(4)) Operand_hoch (.D(D_EIN), .en(O2H_WE), .Q(O2H), .clk(CLK));  // open: clr
  Register #(.width(4)) Operand_tief (.D(D_EIN), .en(O2L_WE), .Q(O2L), .clk(CLK));  // open: clr
  Register #(.width(1)) Zyklus2 (.D(C2_D), .en(C2_WE), .Q(C2), .clk(CLK));  // open: clr

  // Notes on the sheet:
  //   Befehlsregister: OPR/OPA in M1/M2 des ersten Zyklus, zweites Befehlswort (O2H/O2L) im zweiten Zyklus.
  //   C2 = zweiter Maschinenzyklus eines Zwei-Wort-Befehls.
endmodule

module Steuerwerk (
  input  [2:0] PH,
  input  [3:0] OPR,
  input  [3:0] OPA,
  input  C2,
  output IRH_WE,
  output IRL_WE,
  output O2H_WE,
  output O2L_WE,
  output PC_WE,
  output PC_WEC,
  output PUSH,
  output [1:0] BSRC,
  output POP,
  output ACC_WE,
  output CY_WE,
  output RF_WES,
  output RF_WEP,
  output RF_DSEL,
  output PAIR0,
  output CMROM,
  output CMRAM,
  output C2_WE,
  output C2_D,
  output DCL_WE,
  output CONDSEL,
  output [2:0] BS,
  output [1:0] CS,
  output [2:0] RS,
  output [2:0] COS,
  output [1:0] PCSEL,
  output [2:0] DOSEL
);

  wire [11:0] buendel_12_1_bus;

  Buendel_12 buendel_12_1 (
    .b0(PH[0]), .b1(PH[1]), .b2(PH[2]), .b3(C2), .b4(OPA[0]), .b5(OPA[1]), .b6(OPA[2]), .b7(OPA[3]),
    .b8(OPR[0]), .b9(OPR[1]), .b10(OPR[2]), .b11(OPR[3]), .bus(buendel_12_1_bus));
  ROM #(.addrWidth(12), .dataWidth(20)) Steuer_Flags (
    .addr(buendel_12_1_bus),
    .data({CONDSEL, DCL_WE, C2_D, C2_WE, CMRAM, CMROM, PAIR0, RF_DSEL, RF_WEP, RF_WES, CY_WE, ACC_WE, POP, PUSH, PC_WEC, PC_WE, O2L_WE, O2H_WE, IRL_WE, IRH_WE}));  // open: sel
  ROM #(.addrWidth(12), .dataWidth(2)) u_BSRC (.addr(buendel_12_1_bus), .data(BSRC));  // open: sel
  ROM #(.addrWidth(12), .dataWidth(3)) u_BS (.addr(buendel_12_1_bus), .data(BS));  // open: sel
  ROM #(.addrWidth(12), .dataWidth(2)) u_CS (.addr(buendel_12_1_bus), .data(CS));  // open: sel
  ROM #(.addrWidth(12), .dataWidth(3)) u_RS (.addr(buendel_12_1_bus), .data(RS));  // open: sel
  ROM #(.addrWidth(12), .dataWidth(3)) u_COS (.addr(buendel_12_1_bus), .data(COS));  // open: sel
  ROM #(.addrWidth(12), .dataWidth(2)) u_PCSEL (.addr(buendel_12_1_bus), .data(PCSEL));  // open: sel
  ROM #(.addrWidth(12), .dataWidth(3)) u_DOSEL (.addr(buendel_12_1_bus), .data(DOSEL));  // open: sel

  // Notes on the sheet:
  //   Steuerwerk: Adresse = OPR<<8 | OPA<<4 | C2<<3 | Phase. Ersetzt den Befehlsdekoder (PLA) des Originals.
  //   C2 = zweiter Maschinenzyklus eines Zwei-Wort-Befehls (JCN FIM FIN JUN JMS ISZ).
  //   Buendel 12
  //   b0
  //   b1
  //   b2
  //   b3
  //   b4
  //   b5
  //   b6
  //   b7
  //   b8
  //   b9
  //   b10
  //   b11
  //   bus
  //   contents of Steuer_Flags (hex, n*v repeats v):
  //   0 0 0 1 12 0 0 10000 11*0 1 12 0 0 10000 11*0 1 12 0 0 10000 11*0 1 12 0 0 10000 11*0 1 12 0 0 10000
  //   11*0 1 12 0 0 10000 11*0 1 12 0 0 10000 11*0 1 12 0 0 10000 11*0 1 12 0 0 10000 11*0 1 12 0 0 10000
  //   11*0 1 12 0 0 10000 11*0 1 12 0 0 10000 11*0 1 12 0 0 10000 11*0 1 12 0 0 10000 11*0 1 12 0 0 10000
  //   11*0 1 12 0 0 10000 11*0 1 12 0 0 30000 0 0 0 4 18 0 0 10020 0 0 0 1 12 0 0 30000 0 0 0 4 18 0 0
  //   10020 0 0 0 1 12 0 0 30000 0 0 0 4 18 0 0 10020 0 0 0 1 12 0 0 30000 0 0 0 4 18 0 0 10020 0 0 0 1 12
  //   0 0 30000 0 0 0 4 18 0 0 10020 0 0 0 1 12 0 0 30000 0 0 0 4 18 0 0 10020 0 0 0 1 12 0 0 30000 0 0 0
  //   4 18 0 0 10020 0 0 0 1 12 0 0 30000 0 0 0 4 18 0 0 10020 0 0 0 1 12 0 0 30000 0 0 0 4 18 0 0 10020 0
  //   0 0 1 12 0 0 30000 0 0 0 4 18 0 0 10020 0 0 0 1 12 0 0 30000 0 0 0 4 18 0 0 10020 0 0 0 1 12 0 0
  //   30000 0 0 0 4 18 0 0 10020 0 0 0 1 12 0 0 30000 0 0 0 4 18 0 0 10020 0 0 0 1 12 0 0 30000 0 0 0 4 18
  //   0 0 10020 0 0 0 1 12 0 0 30000 0 0 0 4 18 0 0 10020 0 0 0 1 12 0 0 30000 0 0 0 4 18 0 0 10020 0 0 0
  //   1 12 0 0 30000 0 0 0 4 18 0 0 10800 0 0 0 1 12 0 c000 10000 11*0 1 12 0 0 30000 0 0 0 4 18 0 0 10800
  //   0 0 0 1 12 0 c000 10000 11*0 1 12 0 0 30000 0 0 0 4 18 0 0 10800 0 0 0 1 12 0 c000 10000 11*0 1 12 0
  //   0 30000 0 0 0 4 18 0 0 10800 0 0 0 1 12 0 c000 10000 11*0 1 12 0 0 30000 0 0 0 4 18 0 0 10800 0 0 0
  //   1 12 0 c000 10000 11*0 1 12 0 0 30000 0 0 0 4 18 0 0 10800 0 0 0 1 12 0 c000 10000 11*0 1 12 0 0
  //   30000 0 0 0 4 18 0 0 10800 0 0 0 1 12 0 c000 10000 11*0 1 12 0 0 30000 0 0 0 4 18 0 0 10800 0 0 0 1
  //   12 0 c000 10000 11*0 1 12 0 0 30000 2000 2000 0 4 8 0 0 10800 0 0 0 1 12 0 0 10010 11*0 1 12 0 0
  //   30000 2000 2000 0 4 8 0 0 10800 0 0 0 1 12 0 0 10010 11*0 1 12 0 0 30000 2000 2000 0 4 8 0 0 10800 0
  //   0 0 1 12 0 0 10010 11*0 1 12 0 0 30000 2000 2000 0 4 8 0 0 10800 0 0 0 1 12 0 0 10010 11*0 1 12 0 0
  //   30000 2000 2000 0 4 8 0 0 10800 0 0 0 1 12 0 0 10010 11*0 1 12 0 0 30000 2000 2000 0 4 8 0 0 10800 0
  //   0 0 1 12 0 0 10010 11*0 1 12 0 0 30000 2000 2000 0 4 8 0 0 10800 0 0 0 1 12 0 0 10010 11*0 1 12 0 0
  //   30000 2000 2000 0 4 8 0 0 10800 0 0 0 1 12 0 0 10010 11*0 1 12 0 0 30000 0 0 0 4 18 0 0 10010 0 0 0
  //   1 12 0 0 30000 0 0 0 4 18 0 0 10010 0 0 0 1 12 0 0 30000 0 0 0 4 18 0 0 10010 0 0 0 1 12 0 0 30000 0
  //   0 0 4 18 0 0 10010 0 0 0 1 12 0 0 30000 0 0 0 4 18 0 0 10010 0 0 0 1 12 0 0 30000 0 0 0 4 18 0 0
  //   10010 0 0 0 1 12 0 0 30000 0 0 0 4 18 0 0 10010 0 0 0 1 12 0 0 30000 0 0 0 4 18 0 0 10010 0 0 0 1 12
  //   0 0 30000 0 0 0 4 18 0 0 10010 0 0 0 1 12 0 0 30000 0 0 0 4 18 0 0 10010 0 0 0 1 12 0 0 30000 0 0 0
  //   4 18 0 0 10010 0 0 0 1 12 0 0 30000 0 0 0 4 18 0 0 10010 0 0 0 1 12 0 0 30000 0 0 0 4 18 0 0 10010 0
  //   0 0 1 12 0 0 30000 0 0 0 4 18 0 0 10010 0 0 0 1 12 0 0 30000 0 0 0 4 18 0 0 10010 0 0 0 1 12 0 0
  //   30000 0 0 0 4 18 0 0 10010 0 0 0 1 12 0 0 30000 0 0 0 4 18 0 0 10050 0 0 0 1 12 0 0 30000 0 0 0 4 18
  //   0 0 10050 0 0 0 1 12 0 0 30000 0 0 0 4 18 0 0 10050 0 0 0 1 12 0 0 30000 0 0 0 4 18 0 0 10050 0 0 0
  //   1 12 0 0 30000 0 0 0 4 18 0 0 10050 0 0 0 1 12 0 0 30000 0 0 0 4 18 0 0 10050 0 0 0 1 12 0 0 30000 0
  //   0 0 4 18 0 0 10050 0 0 0 1 12 0 0 30000 0 0 0 4 18 0 0 10050 0 0 0 1 12 0 0 30000 0 0 0 4 18 0 0
  //   10050 0 0 0 1 12 0 0 30000 0 0 0 4 18 0 0 10050 0 0 0 1 12 0 0 30000 0 0 0 4 18 0 0 10050 0 0 0 1 12
  //   0 0 30000 0 0 0 4 18 0 0 10050 0 0 0 1 12 0 0 30000 0 0 0 4 18 0 0 10050 0 0 0 1 12 0 0 30000 0 0 0
  //   4 18 0 0 10050 0 0 0 1 12 0 0 30000 0 0 0 4 18 0 0 10050 0 0 0 1 12 0 0 30000 0 0 0 4 18 0 0 10050 0
  //   0 0 1 12 0 0 11400 11*0 1 12 0 0 11400 11*0 1 12 0 0 11400 11*0 1 12 0 0 11400 11*0 1 12 0 0 11400
  //   11*0 1 12 0 0 11400 11*0 1 12 0 0 11400 11*0 1 12 0 0 11400 11*0 1 12 0 0 11400 11*0 1 12 0 0 11400
  //   11*0 1 12 0 0 11400 11*0 1 12 0 0 11400 11*0 1 12 0 0 11400 11*0 1 12 0 0 11400 11*0 1 12 0 0 11400
  //   11*0 1 12 0 0 11400 11*0 1 12 0 0 30000 0 0 0 4 18 0 0 91420 0 0 0 1 12 0 0 30000 0 0 0 4 18 0 0
  //   91420 0 0 0 1 12 0 0 30000 0 0 0 4 18 0 0 91420 0 0 0 1 12 0 0 30000 0 0 0 4 18 0 0 91420 0 0 0 1 12
  //   0 0 30000 0 0 0 4 18 0 0 91420 0 0 0 1 12 0 0 30000 0 0 0 4 18 0 0 91420 0 0 0 1 12 0 0 30000 0 0 0
  //   4 18 0 0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
  //   contents of BSRC (hex, n*v repeats v):
  //   3079*0 2 15*0 2 15*0 2 15*0 2 15*0 2 15*0 2 15*0 2 15*0 2 15*0 2 15*0 2 15*0 2 15*0 2 15*0 2 15*0 2
  //   15*0 2 15*0 2 15*0 2 15*0 2 15*0 2 15*0 2 15*0 2 15*0 2 15*0 2 15*0 2 15*0 2 15*0 2 15*0 2 15*0 2
  //   15*0 2 15*0 2 15*0 2 15*0 2 142*0 1 15*0 1 15*0 1 15*0 1 15*0 1 15*0 1 15*0 1 15*0 1 16*0 3
  //   contents of BS (hex, n*v repeats v):
  //   2311*0 1 15*0 1 15*0 1 15*0 1 15*0 1 15*0 1 15*0 1 15*0 1 15*0 1 15*0 1 15*0 1 15*0 1 15*0 1 15*0 1
  //   15*0 1 15*0 1 1166*0 1 160*0 2 95*0 3 47*0 4
  //   contents of CS (hex, n*v repeats v):
  //   2311*0 1 15*0 1 15*0 1 15*0 1 15*0 1 15*0 1 15*0 1 15*0 1 15*0 1 15*0 1 15*0 1 15*0 1 15*0 1 15*0 1
  //   15*0 1 15*0 1 1166*0 1 160*0 3 95*0 2 47*0 2
  //   contents of RS (hex, n*v repeats v):
  //   2567*0 1 15*0 1 15*0 1 15*0 1 15*0 1 15*0 1 15*0 1 15*0 1 15*0 1 15*0 1 15*0 1 15*0 1 15*0 1 15*0 1
  //   15*0 1 15*0 1 15*0 1 15*0 1 15*0 1 15*0 1 15*0 1 15*0 1 15*0 1 15*0 1 15*0 1 15*0 1 15*0 1 15*0 1
  //   15*0 1 15*0 1 15*0 1 15*0 1 15*0 1 15*0 1 15*0 1 15*0 1 15*0 1 15*0 1 15*0 1 15*0 1 15*0 1 15*0 1
  //   15*0 1 15*0 1 15*0 1 15*0 1 15*0 1 15*0 1 15*0 1 15*0 1 15*0 1 15*0 1 15*0 1 15*0 1 15*0 1 15*0 1
  //   15*0 1 15*0 1 15*0 1 15*0 1 15*0 1 15*0 1 15*0 1 15*0 1 158*0 1 15*0 1 31*0 1 15*0 1 15*0 1 15*0 1
  //   16*0 1 63*0 2 15*0 3 15*0 4 15*0 5 31*0 6 47*0 7
  //   contents of COS (hex, n*v repeats v):
  //   3847*0 3 15*0 3 31*0 5 31*0 1 15*0 2 15*0 3 31*0 3 15*0 4 15*0 6
  //   contents of PCSEL (hex, n*v repeats v):
  //   271*0 1 15*0 1 15*0 1 15*0 1 15*0 1 15*0 1 15*0 1 15*0 1 15*0 1 15*0 1 15*0 1 15*0 1 15*0 1 15*0 1
  //   15*0 1 15*0 1 279*0 3 31*0 3 31*0 3 31*0 3 31*0 3 31*0 3 31*0 3 31*0 3 23*0 2 15*0 2 15*0 2 15*0 2
  //   15*0 2 15*0 2 15*0 2 15*0 2 15*0 2 15*0 2 15*0 2 15*0 2 15*0 2 15*0 2 15*0 2 15*0 2 15*0 2 15*0 2
  //   15*0 2 15*0 2 15*0 2 15*0 2 15*0 2 15*0 2 15*0 2 15*0 2 15*0 2 15*0 2 15*0 2 15*0 2 15*0 2 15*0 2
  //   271*0 1 15*0 1 15*0 1 15*0 1 15*0 1 15*0 1 15*0 1 15*0 1 15*0 1 15*0 1 15*0 1 15*0 1 15*0 1 15*0 1
  //   15*0 1 15*0 1
  //   contents of DOSEL (hex, n*v repeats v):
  //   1 2 3 13*0 1 2 3 13*0 1 2 3 13*0 1 2 3 13*0 1 2 3 13*0 1 2 3 13*0 1 2 3 13*0 1 2 3 13*0 1 2 3 13*0 1
  //   2 3 13*0 1 2 3 13*0 1 2 3 13*0 1 2 3 13*0 1 2 3 13*0 1 2 3 13*0 1 2 3 13*0 1 2 3 5*0 1 2 3 5*0 1 2 3
  //   5*0 1 2 3 5*0 1 2 3 5*0 1 2 3 5*0 1 2 3 5*0 1 2 3 5*0 1 2 3 5*0 1 2 3 5*0 1 2 3 5*0 1 2 3 5*0 1 2 3
  //   5*0 1 2 3 5*0 1 2 3 5*0 1 2 3 5*0 1 2 3 5*0 1 2 3 5*0 1 2 3 5*0 1 2 3 5*0 1 2 3 5*0 1 2 3 5*0 1 2 3
  //   5*0 1 2 3 5*0 1 2 3 5*0 1 2 3 5*0 1 2 3 5*0 1 2 3 5*0 1 2 3 5*0 1 2 3 5*0 1 2 3 5*0 1 2 3 5*0 1 2 3
  //   5*0 1 2 3 5*0 1 2 3 0 0 0 5 6 8*0 1 2 3 5*0 1 2 3 5*0 1 2 3 0 0 0 5 6 8*0 1 2 3 5*0 1 2 3 5*0 1 2 3
  //   0 0 0 5 6 8*0 1 2 3 5*0 1 2 3 5*0 1 2 3 0 0 0 5 6 8*0 1 2 3 5*0 1 2 3 5*0 1 2 3 0 0 0 5 6 8*0 1 2 3
  //   5*0 1 2 3 5*0 1 2 3 0 0 0 5 6 8*0 1 2 3 5*0 1 2 3 5*0 1 2 3 0 0 0 5 6 8*0 1 2 3 5*0 1 2 3 5*0 1 2 3
  //   0 0 0 5 6 8*0 1 2 3 5*0 6 5 3 5*0 1 2 3 13*0 1 2 3 5*0 6 5 3 5*0 1 2 3 13*0 1 2 3 5*0 6 5 3 5*0 1 2
  //   3 13*0 1 2 3 5*0 6 5 3 5*0 1 2 3 13*0 1 2 3 5*0 6 5 3 5*0 1 2 3 13*0 1 2 3 5*0 6 5 3 5*0 1 2 3 13*0
  //   1 2 3 5*0 6 5 3 5*0 1 2 3 13*0 1 2 3 5*0 6 5 3 5*0 1 2 3 13*0 1 2 3 5*0 1 2 3 5*0 1 2 3 5*0 1 2 3
  //   5*0 1 2 3 5*0 1 2 3 5*0 1 2 3 5*0 1 2 3 5*0 1 2 3 5*0 1 2 3 5*0 1 2 3 5*0 1 2 3 5*0 1 2 3 5*0 1 2 3
  //   5*0 1 2 3 5*0 1 2 3 5*0 1 2 3 5*0 1 2 3 5*0 1 2 3 5*0 1 2 3 5*0 1 2 3 5*0 1 2 3 5*0 1 2 3 5*0 1 2 3
  //   5*0 1 2 3 5*0 1 2 3 5*0 1 2 3 5*0 1 2 3 5*0 1 2 3 5*0 1 2 3 5*0 1 2 3 5*0 1 2 3 5*0 1 2 3 5*0 1 2 3
  //   5*0 1 2 3 5*0 1 2 3 5*0 1 2 3 5*0 1 2 3 5*0 1 2 3 5*0 1 2 3 5*0 1 2 3 5*0 1 2 3 5*0 1 2 3 5*0 1 2 3
  //   5*0 1 2 3 5*0 1 2 3 5*0 1 2 3 5*0 1 2 3 5*0 1 2 3 5*0 1 2 3 5*0 1 2 3 5*0 1 2 3 5*0 1 2 3 5*0 1 2 3
  //   5*0 1 2 3 5*0 1 2 3 5*0 1 2 3 5*0 1 2 3 5*0 1 2 3 5*0 1 2 3 5*0 1 2 3 5*0 1 2 3 5*0 1 2 3 5*0 1 2 3
  //   5*0 1 2 3 13*0 1 2 3 13*0 1 2 3 13*0 1 2 3 13*0 1 2 3 13*0 1 2 3 13*0 1 2 3 13*0 1 2 3 13*0 1 2 3
  //   13*0 1 2 3 13*0 1 2 3 13*0 1 2 3 13*0 1 2 3 13*0 1 2 3 13*0 1 2 3 13*0 1 2 3 13*0 1 2 3 5*0 1 2 3
  //   5*0 1 2 3 5*0 1 2 3 5*0 1 2 3 5*0 1 2 3 5*0 1 2 3 5*0 1 2 3 5*0 1 2 3 5*0 1 2 3 5*0 1 2 3 5*0 1 2 3
  //   5*0 1 2 3 5*0 1 2 3 5*0 1 2 3 5*0 1 2 3 5*0 1 2 3 5*0 1 2 3 5*0 1 2 3 5*0 1 2 3 5*0 1 2 3 5*0 1 2 3
  //   5*0 1 2 3 5*0 1 2 3 5*0 1 2 3 5*0 1 2 3 5*0 1 2 3 5*0 1 2 3 5*0 1 2 3 5*0 1 2 3 5*0 1 2 3 5*0 1 2 3
  //   5*0 1 2 3 13*0 1 2 3 13*0 1 2 3 13*0 1 2 3 13*0 1 2 3 13*0 1 2 3 13*0 1 2 3 13*0 1 2 3 13*0 1 2 3
  //   13*0 1 2 3 13*0 1 2 3 13*0 1 2 3 13*0 1 2 3 13*0 1 2 3 13*0 1 2 3 13*0 1 2 3 13*0 1 2 3 13*0 1 2 3
  //   13*0 1 2 3 13*0 1 2 3 13*0 1 2 3 13*0 1 2 3 13*0 1 2 3 13*0 1 2 3 13*0 1 2 3 13*0 1 2 3 13*0 1 2 3
  //   13*0 1 2 3 13*0 1 2 3 13*0 1 2 3 13*0 1 2 3 13*0 1 2 3 13*0 1 2 3 13*0 1 2 3 13*0 1 2 3 13*0 1 2 3
  //   13*0 1 2 3 13*0 1 2 3 13*0 1 2 3 13*0 1 2 3 13*0 1 2 3 13*0 1 2 3 13*0 1 2 3 13*0 1 2 3 13*0 1 2 3
  //   13*0 1 2 3 13*0 1 2 3 13*0 1 2 3 13*0 1 2 3 13*0 1 2 3 13*0 1 2 3 13*0 1 2 3 13*0 1 2 3 13*0 1 2 3
  //   13*0 1 2 3 13*0 1 2 3 13*0 1 2 3 13*0 1 2 3 13*0 1 2 3 13*0 1 2 3 13*0 1 2 3 13*0 1 2 3 13*0 1 2 3
  //   13*0 1 2 3 13*0 1 2 3 13*0 1 2 3 13*0 1 2 3 13*0 1 2 3 13*0 1 2 3 13*0 1 2 3 13*0 1 2 3 13*0 1 2 3
  //   13*0 1 2 3 13*0 1 2 3 13*0 1 2 3 13*0 1 2 3 13*0 1 2 3 13*0 1 2 3 13*0 1 2 3 13*0 1 2 3 13*0 1 2 3
  //   13*0 1 2 3 13*0 1 2 3 13*0 1 2 3 13*0 1 2 3 13*0 1 2 3 13*0 1 2 3 13*0 1 2 3 13*0 1 2 3 13*0 1 2 3
  //   13*0 1 2 3 13*0 1 2 3 13*0 1 2 3 13*0 1 2 3 13*0 1 2 3 13*0 1 2 3 13*0 1 2 3 0 0 0 4 9*0 1 2 3 0 0 0
  //   4 9*0 1 2 3 0 0 0 4 9*0 1 2 3 0 0 0 4 9*0 1 2 3 0 0 0 4 9*0 1 2 3 0 0 0 4 9*0 1 2 3 0 0 0 4 9*0 1 2
  //   3 0 0 0 4 9*0 1 2 3 13*0 1 2 3 13*0 1 2 3 13*0 1 2 3 13*0 1 2 3 13*0 1 2 3 13*0 1 2 3 13*0 1 2 3
  //   13*0 1 2 3 13*0 1 2 3 13*0 1 2 3 13*0 1 2 3 13*0 1 2 3 13*0 1 2 3 13*0 1 2 3 13*0 1 2 3 13*0 1 2 3
  //   13*0 1 2 3 13*0 1 2 3 13*0 1 2 3 13*0 1 2 3 13*0 1 2 3 13*0 1 2 3 13*0 1 2 3
endmodule

module Indexregister (
  input  [3:0] OPA,
  input  PAIR0,
  input  RF_WES,
  input  [3:0] AKKU,
  input  RF_DSEL,
  input  RF_WEP,
  input  [3:0] O2H,
  input  [3:0] O2L,
  input  CLK,
  output [7:0] P0,
  output R_VOLL,
  output [3:0] RSEL,
  output [7:0] P1,
  output [7:0] P2,
  output [3:0] REVEN,
  output [7:0] P3,
  output [3:0] RODD,
  output [7:0] P4,
  output [7:0] P5,
  output [7:0] P6,
  output [7:0] P7
);

  wire and_1_out, and_2_out, and_3_out, dekoder_3zu8_1_y0, dekoder_3zu8_1_y1, dekoder_3zu8_1_y2,
       dekoder_3zu8_1_y3, dekoder_3zu8_1_y4, dekoder_3zu8_1_y5, dekoder_3zu8_1_y6, dekoder_3zu8_1_y7,
       dekoder_3zu8_2_y0, dekoder_3zu8_2_y1, dekoder_3zu8_2_y2, dekoder_3zu8_2_y3, dekoder_3zu8_2_y4,
       dekoder_3zu8_2_y5, dekoder_3zu8_2_y6, dekoder_3zu8_2_y7, not_1_out, or_1_out, or_2_out;
  wire [2:0] buendel_3_1_bus, multiplexer_1_out;
  wire [3:0] adder_1_out, multiplexer_4_out, multiplexer_5_out, multiplexer_6_out, R0_q, R1_q, R2_q, R3_q,
       R4_q, R5_q, R6_q, R7_q, R8_q, R9_q, R10_q, R11_q, R12_q, R13_q, R14_q, R15_q;

  Buendel_3 buendel_3_1 (.b0(OPA[1]), .b1(OPA[2]), .b2(OPA[3]), .bus(buendel_3_1_bus));
  and and_1 (and_1_out, OPA[0], OPA[0]);
  not not_1 (not_1_out, and_1_out);
  Multiplexer #(.select(1), .enable("false"), .width(3)) multiplexer_1 (
    .in0(buendel_3_1_bus), .in1(3'b000), .out(multiplexer_1_out), .sel(PAIR0));
  and and_2 (and_2_out, RF_WES, and_1_out);
  and and_3 (and_3_out, RF_WES, not_1_out);
  or or_1 (or_1_out, RF_WEP, and_2_out);
  or or_2 (or_2_out, RF_WEP, and_3_out);
  Dekoder_3zu8 dekoder_3zu8_1 (
    .A(multiplexer_1_out), .EN(or_1_out), .Y0(dekoder_3zu8_1_y0), .Y1(dekoder_3zu8_1_y1),
    .Y2(dekoder_3zu8_1_y2), .Y7(dekoder_3zu8_1_y7), .Y3(dekoder_3zu8_1_y3), .Y4(dekoder_3zu8_1_y4),
    .Y5(dekoder_3zu8_1_y5), .Y6(dekoder_3zu8_1_y6));
  Dekoder_3zu8 dekoder_3zu8_2 (
    .A(multiplexer_1_out), .EN(or_2_out), .Y0(dekoder_3zu8_2_y0), .Y1(dekoder_3zu8_2_y1),
    .Y2(dekoder_3zu8_2_y2), .Y7(dekoder_3zu8_2_y7), .Y3(dekoder_3zu8_2_y3), .Y4(dekoder_3zu8_2_y4),
    .Y5(dekoder_3zu8_2_y5), .Y6(dekoder_3zu8_2_y6));
  Register #(.width(4)) R0 (.D(multiplexer_5_out), .en(dekoder_3zu8_2_y0), .Q(R0_q), .clk(CLK));  // open: clr
  Multiplexer #(.select(3), .enable("false"), .width(4)) multiplexer_2 (
    .in0(R0_q), .in1(R2_q), .in2(R4_q), .in3(R6_q), .in4(R8_q), .in5(R10_q), .in6(R12_q), .in7(R14_q),
    .out(REVEN), .sel(multiplexer_1_out));
  Multiplexer #(.select(1), .enable("false"), .width(4)) multiplexer_3 (
    .in0(REVEN), .in1(RODD), .out(RSEL), .sel(and_1_out));
  Adder #(.width(4)) adder_1 (.a(RSEL), .b(4'b0000), .out(adder_1_out), .cin(1'b1), .cout(R_VOLL));
  Multiplexer #(.select(1), .enable("false"), .width(4)) multiplexer_4 (
    .in0(AKKU), .in1(adder_1_out), .out(multiplexer_4_out), .sel(RF_DSEL));
  Multiplexer #(.select(1), .enable("false"), .width(4)) multiplexer_5 (
    .in0(multiplexer_4_out), .in1(O2H), .out(multiplexer_5_out), .sel(RF_WEP));
  Multiplexer #(.select(1), .enable("false"), .width(4)) multiplexer_6 (
    .in0(multiplexer_4_out), .in1(O2L), .out(multiplexer_6_out), .sel(RF_WEP));
  Register #(.width(4)) R1 (.D(multiplexer_6_out), .en(dekoder_3zu8_1_y0), .Q(R1_q), .clk(CLK));  // open: clr
  Register #(.width(4)) R2 (.D(multiplexer_5_out), .en(dekoder_3zu8_2_y1), .Q(R2_q), .clk(CLK));  // open: clr
  Register #(.width(4)) R3 (.D(multiplexer_6_out), .en(dekoder_3zu8_1_y1), .Q(R3_q), .clk(CLK));  // open: clr
  Register #(.width(4)) R4 (.D(multiplexer_5_out), .en(dekoder_3zu8_2_y2), .Q(R4_q), .clk(CLK));  // open: clr
  Register #(.width(4)) R5 (.D(multiplexer_6_out), .en(dekoder_3zu8_1_y2), .Q(R5_q), .clk(CLK));  // open: clr
  Register #(.width(4)) R6 (.D(multiplexer_5_out), .en(dekoder_3zu8_2_y3), .Q(R6_q), .clk(CLK));  // open: clr
  Register #(.width(4)) R7 (.D(multiplexer_6_out), .en(dekoder_3zu8_1_y3), .Q(R7_q), .clk(CLK));  // open: clr
  Register #(.width(4)) R8 (.D(multiplexer_5_out), .en(dekoder_3zu8_2_y4), .Q(R8_q), .clk(CLK));  // open: clr
  Register #(.width(4)) R9 (.D(multiplexer_6_out), .en(dekoder_3zu8_1_y4), .Q(R9_q), .clk(CLK));  // open: clr
  Register #(.width(4)) R10 (.D(multiplexer_5_out), .en(dekoder_3zu8_2_y5), .Q(R10_q), .clk(CLK));  // open: clr
  Register #(.width(4)) R11 (.D(multiplexer_6_out), .en(dekoder_3zu8_1_y5), .Q(R11_q), .clk(CLK));  // open: clr
  Register #(.width(4)) R12 (.D(multiplexer_5_out), .en(dekoder_3zu8_2_y6), .Q(R12_q), .clk(CLK));  // open: clr
  Register #(.width(4)) R13 (.D(multiplexer_6_out), .en(dekoder_3zu8_1_y6), .Q(R13_q), .clk(CLK));  // open: clr
  Register #(.width(4)) R14 (.D(multiplexer_5_out), .en(dekoder_3zu8_2_y7), .Q(R14_q), .clk(CLK));  // open: clr
  Register #(.width(4)) R15 (.D(multiplexer_6_out), .en(dekoder_3zu8_1_y7), .Q(R15_q), .clk(CLK));  // open: clr
  Multiplexer #(.select(3), .enable("false"), .width(4)) multiplexer_7 (
    .in0(R1_q), .in1(R3_q), .in2(R5_q), .in3(R7_q), .in4(R9_q), .in5(R11_q), .in6(R13_q), .in7(R15_q),
    .out(RODD), .sel(multiplexer_1_out));
  Buendel_8 buendel_8_1 (
    .b0(R1_q[0]), .b1(R1_q[1]), .b2(R1_q[2]), .b3(R1_q[3]), .b4(R0_q[0]), .b5(R0_q[1]), .b6(R0_q[2]),
    .b7(R0_q[3]), .bus(P0));
  Buendel_8 buendel_8_2 (
    .b0(R3_q[0]), .b1(R3_q[1]), .b2(R3_q[2]), .b3(R3_q[3]), .b4(R2_q[0]), .b5(R2_q[1]), .b6(R2_q[2]),
    .b7(R2_q[3]), .bus(P1));
  Buendel_8 buendel_8_3 (
    .b0(R5_q[0]), .b1(R5_q[1]), .b2(R5_q[2]), .b3(R5_q[3]), .b4(R4_q[0]), .b5(R4_q[1]), .b6(R4_q[2]),
    .b7(R4_q[3]), .bus(P2));
  Buendel_8 buendel_8_4 (
    .b0(R7_q[0]), .b1(R7_q[1]), .b2(R7_q[2]), .b3(R7_q[3]), .b4(R6_q[0]), .b5(R6_q[1]), .b6(R6_q[2]),
    .b7(R6_q[3]), .bus(P3));
  Buendel_8 buendel_8_5 (
    .b0(R9_q[0]), .b1(R9_q[1]), .b2(R9_q[2]), .b3(R9_q[3]), .b4(R8_q[0]), .b5(R8_q[1]), .b6(R8_q[2]),
    .b7(R8_q[3]), .bus(P4));
  Buendel_8 buendel_8_6 (
    .b0(R11_q[0]), .b1(R11_q[1]), .b2(R11_q[2]), .b3(R11_q[3]), .b4(R10_q[0]), .b5(R10_q[1]), .b6(R10_q[2]),
    .b7(R10_q[3]), .bus(P5));
  Buendel_8 buendel_8_7 (
    .b0(R13_q[0]), .b1(R13_q[1]), .b2(R13_q[2]), .b3(R13_q[3]), .b4(R12_q[0]), .b5(R12_q[1]), .b6(R12_q[2]),
    .b7(R12_q[3]), .bus(P6));
  Buendel_8 buendel_8_8 (
    .b0(R15_q[0]), .b1(R15_q[1]), .b2(R15_q[2]), .b3(R15_q[3]), .b4(R14_q[0]), .b5(R14_q[1]), .b6(R14_q[2]),
    .b7(R14_q[3]), .bus(P7));

  // Notes on the sheet:
  //   16 Indexregister R0..R15 zu je 4 Bit, als 8 Paare organisiert (gerade = oberes Nibble).
  //   RF_WES schreibt ein Register (Akku bzw. Register+1 fuer INC/ISZ), RF_WEP ein Paar aus O2H/O2L (FIM, FIN).
  //   PAIR0 waehlt Paar 0 (Adresse fuer FIN), sonst OPA. R_VOLL = Register war 15 (ISZ springt dann nicht).
  //   Buendel 3
  //   b0
  //   b1
  //   bus
  //   b2
  //   Dekoder 3zu8
  //   Y0
  //   Y1
  //   Y2
  //   A
  //   Y7
  //   EN
  //   Y3
  //   Y4
  //   Y5
  //   Y6
  //   Dekoder 3zu8
  //   Y0
  //   Y1
  //   Y2
  //   A
  //   Y7
  //   EN
  //   Y3
  //   Y4
  //   Y5
  //   Y6
  //   Buendel 8
  //   b0
  //   b1
  //   b2
  //   b3
  //   bus
  //   b4
  //   b5
  //   b6
  //   b7
  //   Buendel 8
  //   b0
  //   b1
  //   b2
  //   b3
  //   bus
  //   b4
  //   b5
  //   b6
  //   b7
  //   Buendel 8
  //   b0
  //   b1
  //   b2
  //   b3
  //   bus
  //   b4
  //   b5
  //   b6
  //   b7
  //   Buendel 8
  //   b0
  //   b1
  //   b2
  //   b3
  //   bus
  //   b4
  //   b5
  //   b6
  //   b7
  //   Buendel 8
  //   b0
  //   b1
  //   b2
  //   b3
  //   bus
  //   b4
  //   b5
  //   b6
  //   b7
  //   Buendel 8
  //   b0
  //   b1
  //   b2
  //   b3
  //   bus
  //   b4
  //   b5
  //   b6
  //   b7
  //   Buendel 8
  //   b0
  //   b1
  //   b2
  //   b3
  //   bus
  //   b4
  //   b5
  //   b6
  //   b7
  //   Buendel 8
  //   b0
  //   b1
  //   b2
  //   b3
  //   bus
  //   b4
  //   b5
  //   b6
  //   b7
endmodule

module Rechenwerk (
  input  ACC_WE,
  input  CLK,
  input  [2:0] BS,
  input  [1:0] CS,
  input  CY_WE,
  input  [2:0] COS,
  input  [2:0] RS,
  input  [3:0] RSEL,
  input  [3:0] D_EIN,
  input  [3:0] OPA,
  input  [1:0] BSRC,
  output [3:0] AKKU,
  output CARRY
);

  wire alu_1_cout;
  wire [3:0] alu_1_res, multiplexer_1_out;

  Register #(.width(4)) u_Akku (.D(alu_1_res), .en(ACC_WE), .Q(AKKU), .clk(CLK));  // open: clr
  Multiplexer #(.select(2), .enable("false"), .width(4)) multiplexer_1 (
    .in0(RSEL), .in1(D_EIN), .in2(OPA), .in3(4'b0000), .out(multiplexer_1_out), .sel(BSRC));
  ALU alu_1 (
    .BS(BS), .B(multiplexer_1_out), .CS(CS), .A(AKKU), .COS(COS), .CY(CARRY), .RS(RS), .COUT(alu_1_cout),
    .RES(alu_1_res));
  Register #(.width(1)) u_Carry (.D(alu_1_cout), .en(CY_WE), .Q(CARRY), .clk(CLK));  // open: clr

  // Notes on the sheet:
  //   Rechenwerk: Operandenwahl B (BSRC: Register, Bus, OPA, 0), ALU, Akkumulator und Carry.
  //   ALU
  //   BS
  //   B
  //   CS
  //   COUT
  //   A
  //   RES
  //   COS
  //   CY
  //   RS
endmodule

module Sprungbedingung (
  input  R_VOLL,
  input  CARRY,
  input  PC_WE,
  input  CONDSEL,
  input  PC_WEC,
  input  [3:0] OPA,
  input  [3:0] AKKU,
  input  TEST,
  output PCWE
);

  wire and_1_out, and_2_out, and_3_out, and_4_out, and_5_out, multiplexer_1_out, not_1_out, not_2_out,
       not_3_out, not_4_out, not_5_out, not_6_out, or_1_out, xor_1_out;

  not not_1 (not_1_out, R_VOLL);
  not not_2 (not_2_out, TEST);
  and and_1 (and_1_out, OPA[1], CARRY);
  not not_3 (not_3_out, AKKU[0]);
  not not_4 (not_4_out, AKKU[1]);
  not not_5 (not_5_out, AKKU[2]);
  not not_6 (not_6_out, AKKU[3]);
  and and_2 (and_2_out, OPA[0], not_2_out);
  and and_3 (and_3_out, not_3_out, not_4_out, not_5_out, not_6_out);
  and and_4 (and_4_out, OPA[2], and_3_out);
  or or_1 (or_1_out, and_4_out, and_1_out, and_2_out);
  xor xor_1 (xor_1_out, or_1_out, OPA[3]);
  Multiplexer #(.select(1), .enable("false")) multiplexer_1 (
    .in0(xor_1_out), .in1(not_1_out), .out(multiplexer_1_out), .sel(CONDSEL));
  and and_5 (and_5_out, PC_WEC, multiplexer_1_out);
  or or_2 (PCWE, PC_WE, and_5_out);

  // Notes on the sheet:
  //   JCN: OPA-Bits 2/1/0 pruefen Akku=0, Carry=1, TEST=0; Bit 3 kehrt um. ISZ springt, solange das Register nicht ueberlaeuft.
endmodule

module Adressstapel (
  input  [3:0] OPA,
  input  PUSH,
  input  POP,
  input  WE,
  input  [1:0] PCSEL,
  input  [3:0] O2H,
  input  [3:0] O2L,
  input  [3:0] REVEN,
  input  [3:0] RODD,
  input  CLK,
  output [3:0] PCL,
  output [3:0] PCH,
  output [1:0] SP,
  output [3:0] PCM
);

  wire adder_2_cout, adder_3_cout, dekoder_2zu4_1_y0, dekoder_2zu4_1_y1, dekoder_2zu4_1_y2,
       dekoder_2zu4_1_y3, or_1_out;
  wire [1:0] adder_1_out, buendel_2_1_bus, multiplexer_1_out;
  wire [3:0] adder_2_out, adder_3_out, adder_4_out, multiplexer_3_out, multiplexer_4_out, multiplexer_5_out,
       S0H_q, S0L_q, S0M_q, S1H_q, S1L_q, S1M_q, S2H_q, S2L_q, S2M_q, S3H_q, S3L_q, S3M_q;

  or or_1 (or_1_out, PUSH, POP);
  Buendel_2 buendel_2_1 (.b0(1'b1), .b1(POP), .bus(buendel_2_1_bus));
  Register #(.width(2)) u_SP (.D(adder_1_out), .en(or_1_out), .Q(SP), .clk(CLK));  // open: clr
  Adder #(.width(2)) adder_1 (.a(SP), .b(buendel_2_1_bus), .out(adder_1_out));  // open: cin, cout
  Multiplexer #(.select(1), .enable("false"), .width(2)) multiplexer_1 (
    .in0(SP), .in1(adder_1_out), .out(multiplexer_1_out), .sel(PUSH));
  Dekoder_2zu4 dekoder_2zu4_1 (
    .A(multiplexer_1_out), .EN(WE), .Y0(dekoder_2zu4_1_y0), .Y1(dekoder_2zu4_1_y1), .Y3(dekoder_2zu4_1_y3),
    .Y2(dekoder_2zu4_1_y2));
  Register #(.width(4)) S0L (.D(multiplexer_3_out), .en(dekoder_2zu4_1_y0), .Q(S0L_q), .clk(CLK));  // open: clr
  Multiplexer #(.select(2), .enable("false"), .width(4)) multiplexer_2 (
    .in0(S0L_q), .in1(S1L_q), .in2(S2L_q), .in3(S3L_q), .out(PCL), .sel(SP));
  Adder #(.width(4)) adder_2 (.a(PCL), .b(4'b0000), .out(adder_2_out), .cin(1'b1), .cout(adder_2_cout));
  Adder #(.width(4)) adder_3 (.a(PCM), .b(4'b0000), .out(adder_3_out), .cin(adder_2_cout), .cout(adder_3_cout));
  Multiplexer #(.select(2), .enable("false"), .width(4)) multiplexer_3 (
    .in0(adder_2_out), .in1(O2L), .in2(O2L), .in3(RODD), .out(multiplexer_3_out), .sel(PCSEL));
  Adder #(.width(4)) adder_4 (.a(PCH), .b(4'b0000), .out(adder_4_out), .cin(adder_3_cout));  // open: cout
  Multiplexer #(.select(2), .enable("false"), .width(4)) multiplexer_4 (
    .in0(adder_3_out), .in1(O2H), .in2(O2H), .in3(REVEN), .out(multiplexer_4_out), .sel(PCSEL));
  Register #(.width(4)) S3L (.D(multiplexer_3_out), .en(dekoder_2zu4_1_y3), .Q(S3L_q), .clk(CLK));  // open: clr
  Register #(.width(4)) S2L (.D(multiplexer_3_out), .en(dekoder_2zu4_1_y2), .Q(S2L_q), .clk(CLK));  // open: clr
  Register #(.width(4)) S1L (.D(multiplexer_3_out), .en(dekoder_2zu4_1_y1), .Q(S1L_q), .clk(CLK));  // open: clr
  Multiplexer #(.select(2), .enable("false"), .width(4)) multiplexer_5 (
    .in0(adder_4_out), .in1(PCH), .in2(OPA), .in3(PCH), .out(multiplexer_5_out), .sel(PCSEL));
  Register #(.width(4)) S3M (.D(multiplexer_4_out), .en(dekoder_2zu4_1_y3), .Q(S3M_q), .clk(CLK));  // open: clr
  Register #(.width(4)) S2M (.D(multiplexer_4_out), .en(dekoder_2zu4_1_y2), .Q(S2M_q), .clk(CLK));  // open: clr
  Register #(.width(4)) S1M (.D(multiplexer_4_out), .en(dekoder_2zu4_1_y1), .Q(S1M_q), .clk(CLK));  // open: clr
  Register #(.width(4)) S0M (.D(multiplexer_4_out), .en(dekoder_2zu4_1_y0), .Q(S0M_q), .clk(CLK));  // open: clr
  Register #(.width(4)) S3H (.D(multiplexer_5_out), .en(dekoder_2zu4_1_y3), .Q(S3H_q), .clk(CLK));  // open: clr
  Register #(.width(4)) S2H (.D(multiplexer_5_out), .en(dekoder_2zu4_1_y2), .Q(S2H_q), .clk(CLK));  // open: clr
  Register #(.width(4)) S1H (.D(multiplexer_5_out), .en(dekoder_2zu4_1_y1), .Q(S1H_q), .clk(CLK));  // open: clr
  Register #(.width(4)) S0H (.D(multiplexer_5_out), .en(dekoder_2zu4_1_y0), .Q(S0H_q), .clk(CLK));  // open: clr
  Multiplexer #(.select(2), .enable("false"), .width(4)) multiplexer_6 (
    .in0(S0M_q), .in1(S1M_q), .in2(S2M_q), .in3(S3M_q), .out(PCM), .sel(SP));
  Multiplexer #(.select(2), .enable("false"), .width(4)) multiplexer_7 (
    .in0(S0H_q), .in1(S1H_q), .in2(S2H_q), .in3(S3H_q), .out(PCH), .sel(SP));

  // Notes on the sheet:
  //   Adressstapel wie im 4004: vier 12-Bit-Adressregister, SP zeigt auf das aktuelle (= Programmzaehler).
  //   JMS: SP+1 und Ziel dort ablegen, BBL: SP-1. Damit drei Unterprogrammebenen; Ueberlauf rotiert wie im Original.
  //   PCSEL: 0 = PC+1, 1 = Seite+O2 (JCN/ISZ), 2 = OPA+O2 (JUN/JMS), 3 = Seite+Registerpaar (JIN).
  //   b0
  //   b1
  //   Buendel 2
  //   bus
  //   A
  //   EN
  //   Dekoder 2zu4
  //   Y0
  //   Y1
  //   Y3
  //   Y2
endmodule

module Busausgabe (
  input  [3:0] PCL,
  input  DCL_WE,
  input  CLK,
  input  [3:0] PCM,
  input  [3:0] PCH,
  input  [3:0] REVEN,
  input  [3:0] RODD,
  input  [2:0] DOSEL,
  input  CMRAM,
  input  [3:0] AKKU,
  input  CMROM,
  output CM_RAM1,
  output [3:0] D_AUS,
  output CM_RAM0,
  output CM_RAM2,
  output CM_RAM3,
  output CM_ROM
);

  wire and_5_out, not_1_out, not_2_out, not_3_out;
  wire [2:0] buendel_3_1_bus, DCL_q;

  Multiplexer #(.select(3), .enable("false"), .width(4)) multiplexer_1 (
    .in0(4'b0000), .in1(PCL), .in2(PCM), .in3(PCH), .in4(AKKU), .in5(REVEN), .in6(RODD), .in7(4'b0000),
    .out(D_AUS), .sel(DOSEL));
  and and_1 (CM_ROM, CMROM, CMROM);
  Buendel_3 buendel_3_1 (.b0(AKKU[0]), .b1(AKKU[1]), .b2(AKKU[2]), .bus(buendel_3_1_bus));
  Register #(.width(3)) DCL (.D(buendel_3_1_bus), .en(DCL_WE), .Q(DCL_q), .clk(CLK));  // open: clr
  not not_1 (not_1_out, DCL_q[0]);
  not not_2 (not_2_out, DCL_q[1]);
  not not_3 (not_3_out, DCL_q[2]);
  and and_2 (CM_RAM1, CMRAM, DCL_q[0]);
  and and_3 (CM_RAM2, CMRAM, DCL_q[1]);
  and and_4 (CM_RAM3, CMRAM, DCL_q[2]);
  and and_5 (and_5_out, not_1_out, not_2_out, not_3_out);
  and and_6 (CM_RAM0, CMRAM, and_5_out);

  // Notes on the sheet:
  //   Busausgabe: DOSEL waehlt, was die CPU auf D0-D3 legt (0, PC-Nibbles, Akku, Registerpaar). DCL waehlt die RAM-Bank.
  //   Buendel 3
  //   b0
  //   b1
  //   b2
  //   bus
endmodule

module Anzeige (
  input  [3:0] PCL,
  input  [3:0] PCM,
  input  [3:0] PCH,
  input  [3:0] OPR,
  input  [3:0] OPA,
  output [11:0] PC,
  output [7:0] IR
);

  Buendel_12 buendel_12_1 (
    .b0(PCL[0]), .b1(PCL[1]), .b2(PCL[2]), .b3(PCL[3]), .b4(PCM[0]), .b5(PCM[1]), .b6(PCM[2]), .b7(PCM[3]),
    .b8(PCH[0]), .b9(PCH[1]), .b10(PCH[2]), .b11(PCH[3]), .bus(PC));
  Buendel_8 buendel_8_1 (
    .b0(OPA[0]), .b1(OPA[1]), .b2(OPA[2]), .b3(OPA[3]), .b4(OPR[0]), .b5(OPR[1]), .b6(OPR[2]), .b7(OPR[3]),
    .bus(IR));

  // Notes on the sheet:
  //   Nur zur Beobachtung: PC als 12-Bit-Wert, Befehl als Byte.
  //   b0
  //   b1
  //   b2
  //   b3
  //   b4
  //   b5
  //   b6
  //   b7
  //   b8
  //   b9
  //   b10
  //   b11
  //   Buendel 8
  //   b0
  //   b1
  //   b2
  //   b3
  //   b4
  //   b5
  //   b6
  //   b7
  //   Buendel 12
  //   bus
  //   bus
endmodule

module CPU_4004 (
  input  [3:0] D_EIN,
  input  CLK,
  input  TEST,
  output [7:0] R0R1,
  output SYNC,
  output [11:0] PC,
  output [7:0] IR,
  output [7:0] R2R3,
  output [7:0] R4R5,
  output [7:0] R6R7,
  output [2:0] PHASE,
  output [7:0] R8R9,
  output [7:0] R10R11,
  output [7:0] R12R13,
  output [7:0] R14R15,
  output CARRY,
  output [3:0] AKKU,
  output [1:0] SP,
  output CM_RAM1,
  output [3:0] D_AUS,
  output CM_RAM0,
  output CM_RAM2,
  output CM_RAM3,
  output CM_ROM
);

  wire befehlsregister_1_c2, indexregister_1_r_voll, sprungbedingung_1_pcwe, steuerwerk_1_acc_we,
       steuerwerk_1_c2_d, steuerwerk_1_c2_we, steuerwerk_1_cmram, steuerwerk_1_cmrom, steuerwerk_1_condsel,
       steuerwerk_1_cy_we, steuerwerk_1_dcl_we, steuerwerk_1_irh_we, steuerwerk_1_irl_we,
       steuerwerk_1_o2h_we, steuerwerk_1_o2l_we, steuerwerk_1_pair0, steuerwerk_1_pc_we, steuerwerk_1_pc_wec,
       steuerwerk_1_pop, steuerwerk_1_push, steuerwerk_1_rf_dsel, steuerwerk_1_rf_wep, steuerwerk_1_rf_wes;
  wire [1:0] steuerwerk_1_bsrc, steuerwerk_1_cs, steuerwerk_1_pcsel;
  wire [2:0] steuerwerk_1_bs, steuerwerk_1_cos, steuerwerk_1_dosel, steuerwerk_1_rs;
  wire [3:0] adressstapel_1_pch, adressstapel_1_pcl, adressstapel_1_pcm, befehlsregister_1_o2h,
       befehlsregister_1_o2l, befehlsregister_1_opa, befehlsregister_1_opr, indexregister_1_reven,
       indexregister_1_rodd, indexregister_1_rsel;

  Taktgeber taktgeber_1 (.CLK(CLK), .SYNC(SYNC), .PH(PHASE));
  Befehlsregister befehlsregister_1 (
    .IRH_WE(steuerwerk_1_irh_we), .IRL_WE(steuerwerk_1_irl_we), .D_EIN(D_EIN), .O2H_WE(steuerwerk_1_o2h_we),
    .CLK(CLK), .O2L_WE(steuerwerk_1_o2l_we), .C2_D(steuerwerk_1_c2_d), .C2_WE(steuerwerk_1_c2_we),
    .OPR(befehlsregister_1_opr), .OPA(befehlsregister_1_opa), .O2H(befehlsregister_1_o2h),
    .O2L(befehlsregister_1_o2l), .C2(befehlsregister_1_c2));
  Steuerwerk steuerwerk_1 (
    .PH(PHASE), .OPR(befehlsregister_1_opr), .OPA(befehlsregister_1_opa), .C2(befehlsregister_1_c2),
    .IRH_WE(steuerwerk_1_irh_we), .IRL_WE(steuerwerk_1_irl_we), .O2H_WE(steuerwerk_1_o2h_we),
    .O2L_WE(steuerwerk_1_o2l_we), .PC_WE(steuerwerk_1_pc_we), .PC_WEC(steuerwerk_1_pc_wec),
    .PUSH(steuerwerk_1_push), .BSRC(steuerwerk_1_bsrc), .POP(steuerwerk_1_pop), .ACC_WE(steuerwerk_1_acc_we),
    .CY_WE(steuerwerk_1_cy_we), .RF_WES(steuerwerk_1_rf_wes), .RF_WEP(steuerwerk_1_rf_wep),
    .RF_DSEL(steuerwerk_1_rf_dsel), .PAIR0(steuerwerk_1_pair0), .CMROM(steuerwerk_1_cmrom),
    .CMRAM(steuerwerk_1_cmram), .C2_WE(steuerwerk_1_c2_we), .C2_D(steuerwerk_1_c2_d),
    .DCL_WE(steuerwerk_1_dcl_we), .CONDSEL(steuerwerk_1_condsel), .BS(steuerwerk_1_bs), .CS(steuerwerk_1_cs),
    .RS(steuerwerk_1_rs), .COS(steuerwerk_1_cos), .PCSEL(steuerwerk_1_pcsel), .DOSEL(steuerwerk_1_dosel));
  Indexregister indexregister_1 (
    .OPA(befehlsregister_1_opa), .PAIR0(steuerwerk_1_pair0), .RF_WES(steuerwerk_1_rf_wes), .AKKU(AKKU),
    .RF_DSEL(steuerwerk_1_rf_dsel), .RF_WEP(steuerwerk_1_rf_wep), .O2H(befehlsregister_1_o2h),
    .O2L(befehlsregister_1_o2l), .CLK(CLK), .P0(R0R1), .R_VOLL(indexregister_1_r_voll),
    .RSEL(indexregister_1_rsel), .P1(R2R3), .P2(R4R5), .REVEN(indexregister_1_reven), .P3(R6R7),
    .RODD(indexregister_1_rodd), .P4(R8R9), .P5(R10R11), .P6(R12R13), .P7(R14R15));
  Rechenwerk rechenwerk_1 (
    .ACC_WE(steuerwerk_1_acc_we), .CLK(CLK), .BS(steuerwerk_1_bs), .CS(steuerwerk_1_cs),
    .CY_WE(steuerwerk_1_cy_we), .COS(steuerwerk_1_cos), .RS(steuerwerk_1_rs), .RSEL(indexregister_1_rsel),
    .D_EIN(D_EIN), .OPA(befehlsregister_1_opa), .BSRC(steuerwerk_1_bsrc), .AKKU(AKKU), .CARRY(CARRY));
  Sprungbedingung sprungbedingung_1 (
    .R_VOLL(indexregister_1_r_voll), .CARRY(CARRY), .PC_WE(steuerwerk_1_pc_we),
    .CONDSEL(steuerwerk_1_condsel), .PC_WEC(steuerwerk_1_pc_wec), .OPA(befehlsregister_1_opa), .AKKU(AKKU),
    .TEST(TEST), .PCWE(sprungbedingung_1_pcwe));
  Adressstapel adressstapel_1 (
    .OPA(befehlsregister_1_opa), .PUSH(steuerwerk_1_push), .POP(steuerwerk_1_pop),
    .WE(sprungbedingung_1_pcwe), .PCSEL(steuerwerk_1_pcsel), .O2H(befehlsregister_1_o2h),
    .O2L(befehlsregister_1_o2l), .REVEN(indexregister_1_reven), .RODD(indexregister_1_rodd), .CLK(CLK),
    .PCL(adressstapel_1_pcl), .PCH(adressstapel_1_pch), .SP(SP), .PCM(adressstapel_1_pcm));
  Busausgabe busausgabe_1 (
    .PCL(adressstapel_1_pcl), .DCL_WE(steuerwerk_1_dcl_we), .CLK(CLK), .PCM(adressstapel_1_pcm),
    .PCH(adressstapel_1_pch), .REVEN(indexregister_1_reven), .RODD(indexregister_1_rodd),
    .DOSEL(steuerwerk_1_dosel), .CMRAM(steuerwerk_1_cmram), .AKKU(AKKU), .CMROM(steuerwerk_1_cmrom),
    .CM_RAM1(CM_RAM1), .D_AUS(D_AUS), .CM_RAM0(CM_RAM0), .CM_RAM2(CM_RAM2), .CM_RAM3(CM_RAM3), .CM_ROM(CM_ROM));
  Anzeige anzeige_1 (
    .PCL(adressstapel_1_pcl), .PCM(adressstapel_1_pcm), .PCH(adressstapel_1_pch),
    .OPR(befehlsregister_1_opr), .OPA(befehlsregister_1_opa), .PC(PC), .IR(IR));

  // Notes on the sheet:
  //   Intel 4004 auf Registertransferebene. Datenbus aufgeteilt: D_EIN (wired-OR aller Bausteine) und D_AUS.
  //   Kein Tristate noetig: jeder Baustein legt 0 an, wenn er nicht treibt; im System werden alle per ODER zusammengefasst.
  //   Taktgeber
  //   CLK
  //   SYNC
  //   PH
  //   Befehlsregister
  //   IRH_WE
  //   IRL_WE
  //   OPR
  //   D_EIN
  //   OPA
  //   O2H_WE
  //   O2H
  //   CLK
  //   O2L
  //   O2L_WE
  //   C2
  //   C2_D
  //   C2_WE
  //   Steuerwerk
  //   IRH_WE
  //   IRL_WE
  //   O2H_WE
  //   O2L_WE
  //   PC_WE
  //   PC_WEC
  //   PUSH
  //   BSRC
  //   POP
  //   ACC_WE
  //   CY_WE
  //   PH
  //   RF_WES
  //   OPR
  //   RF_WEP
  //   OPA
  //   RF_DSEL
  //   C2
  //   PAIR0
  //   CMROM
  //   CMRAM
  //   C2_WE
  //   C2_D
  //   DCL_WE
  //   CONDSEL
  //   BS
  //   CS
  //   RS
  //   COS
  //   PCSEL
  //   DOSEL
  //   Indexregister
  //   P0
  //   OPA
  //   R_VOLL
  //   PAIR0
  //   RSEL
  //   RF_WES
  //   P1
  //   AKKU
  //   P2
  //   RF_DSEL
  //   REVEN
  //   RF_WEP
  //   P3
  //   O2H
  //   RODD
  //   O2L
  //   P4
  //   CLK
  //   P5
  //   P6
  //   P7
  //   Rechenwerk
  //   ACC_WE
  //   CLK
  //   BS
  //   CS
  //   CY_WE
  //   AKKU
  //   COS
  //   CARRY
  //   RS
  //   RSEL
  //   D_EIN
  //   OPA
  //   BSRC
  //   Sprungbedingung
  //   R_VOLL
  //   CARRY
  //   PC_WE
  //   CONDSEL
  //   PCWE
  //   PC_WEC
  //   OPA
  //   AKKU
  //   TEST
  //   Adressstapel
  //   OPA
  //   PUSH
  //   POP
  //   WE
  //   PCL
  //   PCSEL
  //   PCH
  //   O2H
  //   SP
  //   O2L
  //   PCM
  //   REVEN
  //   RODD
  //   CLK
  //   Busausgabe
  //   PCL
  //   DCL_WE
  //   CLK
  //   CM_RAM1
  //   PCM
  //   D_AUS
  //   PCH
  //   CM_RAM0
  //   REVEN
  //   CM_RAM2
  //   RODD
  //   CM_RAM3
  //   DOSEL
  //   CM_ROM
  //   CMRAM
  //   AKKU
  //   CMROM
  //   Anzeige
  //   PCL
  //   PCM
  //   PCH
  //   OPR
  //   OPA
  //   PC
  //   IR
endmodule

module Peripherie_Phase (
  input  SYNC,
  input  CLK,
  output T0,
  output T1,
  output T2,
  output T7,
  output T3,
  output T4,
  output T5,
  output T6
);

  wire [2:0] adder_1_out, multiplexer_1_out, Phase_q;

  Register #(.width(3)) Phase (.D(multiplexer_1_out), .Q(Phase_q), .clk(CLK));  // open: en, clr
  Adder #(.width(3)) adder_1 (.a(Phase_q), .b(3'b001), .out(adder_1_out));  // open: cin, cout
  Dekoder_3zu8 dekoder_3zu8_1 (
    .A(Phase_q), .EN(1'b1), .Y0(T0), .Y1(T1), .Y2(T2), .Y7(T7), .Y3(T3), .Y4(T4), .Y5(T5), .Y6(T6));
  Multiplexer #(.select(1), .enable("false"), .width(3)) multiplexer_1 (
    .in0(adder_1_out), .in1(3'b000), .out(multiplexer_1_out), .sel(SYNC));

  // Notes on the sheet:
  //   Eigener Phasenzaehler der Peripheriebausteine, mit SYNC (X3) auf A1 gesetzt - wie in 4001/4002.
  //   Dekoder 3zu8
  //   A
  //   EN
  //   Y0
  //   Y1
  //   Y2
  //   Y7
  //   Y3
  //   Y4
  //   Y5
  //   Y6
endmodule

module ROM_4001 (
  input  SYNC,
  input  [3:0] BUS,
  input  CLK,
  input  CM_ROM,
  input  [3:0] PORT_EIN,
  input  [7:0] ROMDATEN,
  output [11:0] ADRESSE,
  output [3:0] PORT_AUS,
  output [3:0] D_AUS
);

  wire and_1_out, and_2_out, and_3_out, and_4_out, and_5_out, and_6_out, Chip0_gewaehlt_q, not_1_out,
       not_2_out, not_3_out, not_4_out, not_5_out, not_6_out, not_7_out, peripherie_phase_1_t0,
       peripherie_phase_1_t1, peripherie_phase_1_t2, peripherie_phase_1_t3, peripherie_phase_1_t4,
       peripherie_phase_1_t5, peripherie_phase_1_t6, peripherie_phase_1_t7;
  wire [3:0] Adr_A1_q, Adr_A2_q, Adr_A3_q, buendel_4_1_bus, buendel_4_2_bus, IO_Befehl_q, multiplexer_1_out,
       multiplexer_2_out, multiplexer_3_out;

  Peripherie_Phase peripherie_phase_1 (
    .SYNC(SYNC), .CLK(CLK), .T0(peripherie_phase_1_t0), .T1(peripherie_phase_1_t1),
    .T2(peripherie_phase_1_t2), .T7(peripherie_phase_1_t7), .T3(peripherie_phase_1_t3),
    .T4(peripherie_phase_1_t4), .T5(peripherie_phase_1_t5), .T6(peripherie_phase_1_t6));
  Multiplexer #(.select(1), .enable("false"), .width(4)) multiplexer_1 (
    .in0(4'b1111), .in1(BUS), .out(multiplexer_1_out), .sel(CM_ROM));
  Register #(.width(4)) Adr_A3 (.D(BUS), .en(peripherie_phase_1_t2), .Q(Adr_A3_q), .clk(CLK));  // open: clr
  Register #(.width(4)) Adr_A2 (.D(BUS), .en(peripherie_phase_1_t1), .Q(Adr_A2_q), .clk(CLK));  // open: clr
  and and_1 (and_1_out, peripherie_phase_1_t6, CM_ROM);
  Register #(.width(4)) Adr_A1 (.D(BUS), .en(peripherie_phase_1_t0), .Q(Adr_A1_q), .clk(CLK));  // open: clr
  not not_1 (not_1_out, BUS[0]);
  not not_2 (not_2_out, BUS[1]);
  not not_3 (not_3_out, BUS[2]);
  not not_4 (not_4_out, BUS[3]);
  Register #(.width(4)) IO_Befehl (
    .D(multiplexer_1_out), .en(peripherie_phase_1_t4), .Q(IO_Befehl_q), .clk(CLK));  // open: clr
  Buendel_4 buendel_4_1 (.b0(ROMDATEN[0]), .b1(ROMDATEN[1]), .b2(ROMDATEN[2]), .b3(ROMDATEN[3]), .bus(buendel_4_1_bus));
  Buendel_4 buendel_4_2 (.b0(ROMDATEN[4]), .b1(ROMDATEN[5]), .b2(ROMDATEN[6]), .b3(ROMDATEN[7]), .bus(buendel_4_2_bus));
  and and_2 (and_2_out, not_1_out, not_2_out, not_3_out, not_4_out);
  Multiplexer #(.select(1), .enable("false"), .width(4)) multiplexer_2 (
    .in0(4'b0000), .in1(buendel_4_2_bus), .out(multiplexer_2_out), .sel(peripherie_phase_1_t3));
  Buendel_12 buendel_12_1 (
    .b0(Adr_A1_q[0]), .b1(Adr_A1_q[1]), .b2(Adr_A1_q[2]), .b3(Adr_A1_q[3]), .b4(Adr_A2_q[0]),
    .b5(Adr_A2_q[1]), .b6(Adr_A2_q[2]), .b7(Adr_A2_q[3]), .b8(Adr_A3_q[0]), .b9(Adr_A3_q[1]),
    .b10(Adr_A3_q[2]), .b11(Adr_A3_q[3]), .bus(ADRESSE));
  not not_5 (not_5_out, IO_Befehl_q[3]);
  Register #(.width(1)) Chip0_gewaehlt (.D(and_2_out), .en(and_1_out), .Q(Chip0_gewaehlt_q), .clk(CLK));  // open: clr
  not not_6 (not_6_out, IO_Befehl_q[0]);
  not not_7 (not_7_out, IO_Befehl_q[2]);
  Multiplexer #(.select(1), .enable("false"), .width(4)) multiplexer_3 (
    .in0(multiplexer_2_out), .in1(buendel_4_1_bus), .out(multiplexer_3_out), .sel(peripherie_phase_1_t4));
  and and_3 (and_3_out, not_6_out, IO_Befehl_q[1], not_7_out, not_5_out);
  and and_4 (and_4_out, not_6_out, IO_Befehl_q[1], not_7_out, IO_Befehl_q[3]);
  and and_5 (and_5_out, peripherie_phase_1_t6, Chip0_gewaehlt_q, and_3_out);
  and and_6 (and_6_out, peripherie_phase_1_t6, Chip0_gewaehlt_q, and_4_out);
  Register #(.width(4)) Ausgabeport (.D(BUS), .en(and_5_out), .Q(PORT_AUS), .clk(CLK));  // open: clr
  Multiplexer #(.select(1), .enable("false"), .width(4)) multiplexer_4 (
    .in0(multiplexer_3_out), .in1(PORT_EIN), .out(D_AUS), .sel(and_6_out));

  // Notes on the sheet:
  //   ROM-Bank (bis 16 x 4001 in einem Speicher): Adresse wird in A1..A3 nibbleweise vom Bus uebernommen,
  //   in M1/M2 wird OPR/OPA ausgegeben. I/O-Port nur fuer Chip 0: SRC mit oberem Nibble 0 waehlt ihn, WRR/RDR.
  //   Peripherie Phase
  //   T0
  //   T1
  //   T2
  //   SYNC
  //   T7
  //   CLK
  //   T3
  //   T4
  //   T5
  //   T6
  //   b0
  //   b1
  //   b2
  //   b3
  //   b0
  //   b1
  //   b2
  //   b3
  //   Buendel 4
  //   bus
  //   Buendel 4
  //   bus
  //   b0
  //   b1
  //   b2
  //   b3
  //   b4
  //   b5
  //   b6
  //   b7
  //   b8
  //   b9
  //   b10
  //   b11
  //   Buendel 12
  //   bus
endmodule

module RAM_4002 (
  input  SYNC,
  input  CM_RAM,
  input  [3:0] BUS,
  input  CLK,
  output [3:0] D_AUS,
  output [3:0] PORT_AUS
);

  wire and_1_out, and_2_out, and_3_out, and_4_out, and_5_out, and_6_out, and_7_out, and_8_out, and_9_out,
       and_10_out, and_11_out, and_12_out, and_13_out, Chip0_gewaehlt_q, IO_aktiv_q, not_1_out, not_2_out,
       not_3_out, not_4_out, not_5_out, not_6_out, not_7_out, peripherie_phase_1_t0, peripherie_phase_1_t1,
       peripherie_phase_1_t2, peripherie_phase_1_t3, peripherie_phase_1_t4, peripherie_phase_1_t5,
       peripherie_phase_1_t6, peripherie_phase_1_t7, SRC_aktiv_q;
  wire [1:0] buendel_2_1_bus, Register_q;
  wire [3:0] buendel_4_1_bus, Hauptzeichen_4x16_data, IO_Befehl_q, multiplexer_1_out, Status_4x4_data,
       Zeichen_q;
  wire [5:0] buendel_6_1_bus;

  Peripherie_Phase peripherie_phase_1 (
    .SYNC(SYNC), .CLK(CLK), .T0(peripherie_phase_1_t0), .T1(peripherie_phase_1_t1),
    .T2(peripherie_phase_1_t2), .T7(peripherie_phase_1_t7), .T3(peripherie_phase_1_t3),
    .T4(peripherie_phase_1_t4), .T5(peripherie_phase_1_t5), .T6(peripherie_phase_1_t6));
  not not_1 (not_1_out, BUS[2]);
  not not_2 (not_2_out, BUS[3]);
  Register #(.width(1)) IO_aktiv (.D(CM_RAM), .en(peripherie_phase_1_t4), .Q(IO_aktiv_q), .clk(CLK));  // open: clr
  and and_1 (and_1_out, peripherie_phase_1_t6, CM_RAM);
  and and_2 (and_2_out, peripherie_phase_1_t4, CM_RAM);
  Buendel_2 buendel_2_1 (.b0(BUS[0]), .b1(BUS[1]), .bus(buendel_2_1_bus));
  Register #(.width(1)) SRC_aktiv (.D(CM_RAM), .en(peripherie_phase_1_t6), .Q(SRC_aktiv_q), .clk(CLK));  // open: clr
  and and_3 (and_3_out, not_2_out, not_1_out);
  Register #(.width(4)) IO_Befehl (.D(BUS), .en(and_2_out), .Q(IO_Befehl_q), .clk(CLK));  // open: clr
  Register #(.width(2)) Register (.D(buendel_2_1_bus), .en(and_1_out), .Q(Register_q), .clk(CLK));  // open: clr
  and and_4 (and_4_out, peripherie_phase_1_t7, SRC_aktiv_q);
  Register #(.width(4)) Zeichen (.D(BUS), .en(and_4_out), .Q(Zeichen_q), .clk(CLK));  // open: clr
  Register #(.width(1)) Chip0_gewaehlt (.D(and_3_out), .en(and_1_out), .Q(Chip0_gewaehlt_q), .clk(CLK));  // open: clr
  not not_3 (not_3_out, IO_Befehl_q[2]);
  and and_5 (and_5_out, peripherie_phase_1_t6, IO_aktiv_q, Chip0_gewaehlt_q);
  not not_4 (not_4_out, IO_Befehl_q[0]);
  not not_5 (not_5_out, IO_Befehl_q[3]);
  Buendel_4 buendel_4_1 (
    .b0(IO_Befehl_q[0]), .b1(IO_Befehl_q[1]), .b2(Register_q[0]), .b3(Register_q[1]), .bus(buendel_4_1_bus));
  not not_6 (not_6_out, IO_Befehl_q[1]);
  and and_6 (and_6_out, IO_Befehl_q[3], IO_Befehl_q[2]);
  and and_7 (and_7_out, not_4_out, IO_Befehl_q[1], not_3_out, IO_Befehl_q[3]);
  and and_8 (and_8_out, IO_Befehl_q[0], not_6_out, not_3_out, not_5_out);
  and and_9 (and_9_out, and_5_out, not_5_out, IO_Befehl_q[2]);
  Buendel_6 buendel_6_1 (
    .b0(Zeichen_q[0]), .b1(Zeichen_q[1]), .b2(Zeichen_q[2]), .b3(Zeichen_q[3]), .b4(Register_q[0]),
    .b5(Register_q[1]), .bus(buendel_6_1_bus));
  and and_10 (and_10_out, not_4_out, not_6_out, not_3_out, not_5_out);
  not not_7 (not_7_out, and_7_out);
  and and_11 (and_11_out, and_5_out, and_8_out);
  and and_12 (and_12_out, and_5_out, and_10_out);
  RAM #(.addrWidth(4), .dataWidth(4), .bus("separate")) Status_4x4 (
    .addr(buendel_4_1_bus), .din(BUS), .data(Status_4x4_data), .str(and_9_out), .clk(CLK));  // open: sel, ld, clr
  and and_13 (and_13_out, and_5_out, IO_Befehl_q[3], not_7_out);
  Register #(.width(4)) Ausgabeport (.D(BUS), .en(and_11_out), .Q(PORT_AUS), .clk(CLK));  // open: clr
  RAM #(.addrWidth(6), .dataWidth(4), .bus("separate")) Hauptzeichen_4x16 (
    .addr(buendel_6_1_bus), .din(BUS), .data(Hauptzeichen_4x16_data), .str(and_12_out), .clk(CLK));  // open: sel, ld, clr
  Multiplexer #(.select(1), .enable("false"), .width(4)) multiplexer_1 (
    .in0(Hauptzeichen_4x16_data), .in1(Status_4x4_data), .out(multiplexer_1_out), .sel(and_6_out));
  Multiplexer #(.select(1), .enable("false"), .width(4)) multiplexer_2 (
    .in0(4'b0000), .in1(multiplexer_1_out), .out(D_AUS), .sel(and_13_out));

  // Notes on the sheet:
  //   Ein 4002 (Bank 0, Chip 0): 4 Register x 16 Hauptzeichen + 4 Statuszeichen, 4-Bit-Ausgabeport.
  //   SRC in X2/X3 waehlt Chip, Register und Zeichen; I/O-Befehle werden in M2 mitgelesen und in X2 ausgefuehrt.
  //   SYNC
  //   CLK
  //   Peripherie Phase
  //   T0
  //   T1
  //   T2
  //   T7
  //   T3
  //   T4
  //   T5
  //   T6
  //   Buendel 2
  //   b0
  //   bus
  //   b1
  //   Buendel 4
  //   b0
  //   b1
  //   bus
  //   b2
  //   b3
  //   Buendel 6
  //   b0
  //   b1
  //   b2
  //   bus
  //   b3
  //   b4
  //   b5
endmodule

module System_4004 (
  input  [3:0] PORT_EIN,
  input  TEST,
  output [7:0] R0R1,
  output [11:0] PC,
  output [7:0] IR,
  output [3:0] ROM_PORT,
  output [7:0] R2R3,
  output [7:0] R4R5,
  output SYNC,
  output [7:0] R6R7,
  output [2:0] PHASE,
  output [7:0] R8R9,
  output [7:0] R10R11,
  output [7:0] R12R13,
  output [7:0] R14R15,
  output [3:0] BUS,
  output CARRY,
  output [3:0] AKKU,
  output [1:0] SP,
  output [3:0] RAM_PORT
);

  wire clock_1_out, cpu_4004_1_cm_ram0, cpu_4004_1_cm_ram1, cpu_4004_1_cm_ram2, cpu_4004_1_cm_ram3,
       cpu_4004_1_cm_rom;
  wire [3:0] cpu_4004_1_d_aus, ram_4002_1_d_aus, rom_4001_1_d_aus;
  wire [7:0] Programm_data;
  wire [11:0] rom_4001_1_adresse;

  Clock clock_1 (.out(clock_1_out));
  CPU_4004 cpu_4004_1 (
    .D_EIN(BUS), .CLK(clock_1_out), .TEST(TEST), .R0R1(R0R1), .SYNC(SYNC), .PC(PC), .IR(IR), .R2R3(R2R3),
    .R4R5(R4R5), .R6R7(R6R7), .PHASE(PHASE), .R8R9(R8R9), .R10R11(R10R11), .R12R13(R12R13), .R14R15(R14R15),
    .CARRY(CARRY), .AKKU(AKKU), .SP(SP), .CM_RAM1(cpu_4004_1_cm_ram1), .D_AUS(cpu_4004_1_d_aus),
    .CM_RAM0(cpu_4004_1_cm_ram0), .CM_RAM2(cpu_4004_1_cm_ram2), .CM_RAM3(cpu_4004_1_cm_ram3),
    .CM_ROM(cpu_4004_1_cm_rom));
  ROM_4001 rom_4001_1 (
    .SYNC(SYNC), .BUS(BUS), .CLK(clock_1_out), .CM_ROM(cpu_4004_1_cm_rom), .PORT_EIN(PORT_EIN),
    .ROMDATEN(Programm_data), .ADRESSE(rom_4001_1_adresse), .PORT_AUS(ROM_PORT), .D_AUS(rom_4001_1_d_aus));
  assign BUS = cpu_4004_1_d_aus | rom_4001_1_d_aus | ram_4002_1_d_aus;  // OR_Gate or_1, 4 bits wide
  ROM #(.addrWidth(12), .dataWidth(8)) Programm (.addr(rom_4001_1_adresse), .data(Programm_data));  // open: sel
  RAM_4002 ram_4002_1 (
    .SYNC(SYNC), .CM_RAM(cpu_4004_1_cm_ram0), .BUS(BUS), .CLK(clock_1_out), .D_AUS(ram_4002_1_d_aus),
    .PORT_AUS(RAM_PORT));

  // Notes on the sheet:
  //   Intel-4004-System: CPU, ROM-Bank (4001) mit Programm-ROM, ein RAM-Chip 4002. Datenbus als wired-OR.
  //   Programm: ROM "Programm" anklicken (Web-Simulator) bzw. Inhalt bearbeiten (Logisim). Ein Befehl = 8 Subzyklen = 16 Taktschritte.
  //   TEST-Pin fuer JCN, PORT_EIN wird mit RDR gelesen (nach SRC auf ROM-Chip 0).
  //   CPU 4004
  //   R0R1
  //   SYNC
  //   PC
  //   IR
  //   R2R3
  //   R4R5
  //   R6R7
  //   PHASE
  //   R8R9
  //   D_EIN
  //   R10R11
  //   CLK
  //   R12R13
  //   TEST
  //   R14R15
  //   CARRY
  //   AKKU
  //   SP
  //   CM_RAM1
  //   D_AUS
  //   CM_RAM0
  //   CM_RAM2
  //   CM_RAM3
  //   CM_ROM
  //   ROM 4001
  //   SYNC
  //   BUS
  //   ADRESSE
  //   CLK
  //   PORT_AUS
  //   CM_ROM
  //   D_AUS
  //   PORT_EIN
  //   ROMDATEN
  //   contents of Programm (hex, n*v repeats v):
  //   20 0 21 d0 b2 d1 b3 f1 a2 83 b3 b2 a3 e2 e1 40 7
  //   SYNC
  //   CM_RAM
  //   BUS
  //   CLK
  //   RAM 4002
  //   D_AUS
  //   PORT_AUS
endmodule
