# Fritzing sketch Z3-1BitRam (saved by Fritzing 1.0.1rc)

parts:
  D1 = Diode [package=diode-1n4148]
  S4 = Momentary Switch [package=ksa_sealed_tac_switch]
  LED3 = smd LED [color="Orange (620nm)" package="0603 [SMD]"]  # not connected
  R3 = Resistor [tolerance=±5% resistance=220 package="2512 [SMD]"]
  8-Channel_Relay1 = 8-Channel 5v Relay Shield [package=relay-8ch5v10a]
  S5 = Momentary Switch [package=ksa_sealed_tac_switch]
  OMRON5 = OMRON PCB Power Relay – G5LE [part_number="G5LE-1\n" package=THT]
  S6 = Momentary Switch [package=ksa_sealed_tac_switch]
  S7 = Momentary Switch [package=ksa_sealed_tac_switch]  # not connected

nets:
  N1: D1.A, OMRON5.COIL2
  N2: D1.C, OMRON5.C
  N3: S4.3, 8-Channel_Relay1.IN1, 8-Channel_Relay1.K1-Off, S5.4
  N4: R3.Pin_1, 8-Channel_Relay1.K1-On
  N5: OMRON5.COIL1, S6.1

custom parts:
  8-Channel 5v Relay Shield: 8 Channel 5v Relay Shield w. 2x SPD-06VDC-SD-C
